// Logisim project CPU.circ as structural Verilog
module main (
);

  wire [3:0] multiplexer_1_out, pc_incr_1_pcout, undriven;

  Register8Bit register8bit_1 ();  // open: in1, out1, Enbl
  Register8Bit register8bit_2 ();  // open: in1, out1, Enbl
  MAR mar_1 (.Out1(undriven), .In1(multiplexer_1_out));
  Multiplexer #(.width(4), .enable("false")) multiplexer_1 (
    .in1(pc_incr_1_pcout), .out(multiplexer_1_out));  // open: in0, sel
  PC_incr pc_incr_1 (.PCIn(undriven), .PCOut(pc_incr_1_pcout));
  MAR mar_2 (.In1(undriven));  // open: Out1
endmodule

module display (
  input  in_1,
  input  in_2,
  input  in_3,
  input  in_4,
  input  in_5,
  input  in_6,
  input  in_7,
  input  in_8
);

  wire bcd_1_out_9, bcd_1_out_10, bcd_1_out_11, bcd_1_out_12, bcd_1_out_13, bcd_1_out_14, bcd_1_out_15,
       bcd_1_out_16, bcd_1_out_17, bcd_1_out_18, digit_1_out_5, digit_1_out_6, digit_1_out_7, digit_1_out_8,
       digit_1_out_9, digit_1_out_10, digit_1_out_11, digit_2_out_5, digit_2_out_6, digit_2_out_7,
       digit_2_out_8, digit_2_out_9, digit_2_out_10, digit_2_out_11, digit_3_out_5, digit_3_out_6,
       digit_3_out_7, digit_3_out_8, digit_3_out_9, digit_3_out_10, digit_3_out_11;

  BCD bcd_1 (
    .in_1(in_1), .in_2(in_2), .in_3(in_3), .in_4(in_4), .in_5(in_5), .in_6(in_6), .in_7(in_7), .in_8(in_8),
    .out_9(bcd_1_out_9), .out_10(bcd_1_out_10), .out_11(bcd_1_out_11), .out_12(bcd_1_out_12),
    .out_13(bcd_1_out_13), .out_14(bcd_1_out_14), .out_15(bcd_1_out_15), .out_16(bcd_1_out_16),
    .out_17(bcd_1_out_17), .out_18(bcd_1_out_18));
  _7_Segment_Display u_7_segment_display_1 (
    .g(digit_1_out_5), .f(digit_1_out_6), .a(digit_1_out_7), .b(digit_1_out_8), .e(digit_1_out_9),
    .d(digit_1_out_10), .c(digit_1_out_11));  // open: dp
  digit digit_1 (
    .out_9(digit_1_out_9), .out_8(digit_1_out_8), .out_7(digit_1_out_7), .out_6(digit_1_out_6),
    .out_5(digit_1_out_5), .in_4(bcd_1_out_10), .in_3(bcd_1_out_9), .out_10(digit_1_out_10),
    .out_11(digit_1_out_11));  // open: in_2, in_1
  _7_Segment_Display u_7_segment_display_2 (
    .g(digit_2_out_5), .f(digit_2_out_6), .a(digit_2_out_7), .b(digit_2_out_8), .e(digit_2_out_9),
    .d(digit_2_out_10), .c(digit_2_out_11));  // open: dp
  digit digit_2 (
    .out_9(digit_2_out_9), .out_8(digit_2_out_8), .out_7(digit_2_out_7), .out_6(digit_2_out_6),
    .out_5(digit_2_out_5), .in_4(bcd_1_out_14), .in_3(bcd_1_out_13), .in_2(bcd_1_out_12),
    .in_1(bcd_1_out_11), .out_10(digit_2_out_10), .out_11(digit_2_out_11));
  _7_Segment_Display u_7_segment_display_3 (
    .g(digit_3_out_5), .f(digit_3_out_6), .a(digit_3_out_7), .b(digit_3_out_8), .e(digit_3_out_9),
    .d(digit_3_out_10), .c(digit_3_out_11));  // open: dp
  digit digit_3 (
    .out_9(digit_3_out_9), .out_8(digit_3_out_8), .out_7(digit_3_out_7), .out_6(digit_3_out_6),
    .out_5(digit_3_out_5), .in_4(bcd_1_out_18), .in_3(bcd_1_out_17), .in_2(bcd_1_out_16),
    .in_1(bcd_1_out_15), .out_10(digit_3_out_10), .out_11(digit_3_out_11));
endmodule

module RAM16 (
  input  addr1,
  input  addr2,
  input  addr3,
  input  addr4,
  input  EnableWrite,
  input  CLK,
  input  b1,
  input  b2,
  input  b3,
  input  b4,
  input  b5,
  input  b6,
  input  b7,
  input  b8,
  output o1,
  output o2,
  output o3,
  output o4,
  output o5,
  output o6,
  output o7,
  output o8
);

  wire and_1_out, and_2_out, and_3_out, and_4_out, and_5_out, and_6_out, and_7_out, and_8_out, and_9_out,
       and_10_out, and_11_out, and_12_out, and_13_out, and_14_out, and_15_out, and_16_out, byte_storage_1_o1,
       byte_storage_1_o2, byte_storage_1_o3, byte_storage_1_o4, byte_storage_1_o5, byte_storage_1_o6,
       byte_storage_1_o7, byte_storage_1_o8, byte_storage_2_o1, byte_storage_2_o2, byte_storage_2_o3,
       byte_storage_2_o4, byte_storage_2_o5, byte_storage_2_o6, byte_storage_2_o7, byte_storage_2_o8,
       byte_storage_3_o1, byte_storage_3_o2, byte_storage_3_o3, byte_storage_3_o4, byte_storage_3_o5,
       byte_storage_3_o6, byte_storage_3_o7, byte_storage_3_o8, byte_storage_4_o1, byte_storage_4_o2,
       byte_storage_4_o3, byte_storage_4_o4, byte_storage_4_o5, byte_storage_4_o6, byte_storage_4_o7,
       byte_storage_4_o8, byte_storage_5_o1, byte_storage_5_o2, byte_storage_5_o3, byte_storage_5_o4,
       byte_storage_5_o5, byte_storage_5_o6, byte_storage_5_o7, byte_storage_5_o8, byte_storage_6_o1,
       byte_storage_6_o2, byte_storage_6_o3, byte_storage_6_o4, byte_storage_6_o5, byte_storage_6_o6,
       byte_storage_6_o7, byte_storage_6_o8, byte_storage_7_o1, byte_storage_7_o2, byte_storage_7_o3,
       byte_storage_7_o4, byte_storage_7_o5, byte_storage_7_o6, byte_storage_7_o7, byte_storage_7_o8,
       byte_storage_8_o1, byte_storage_8_o2, byte_storage_8_o3, byte_storage_8_o4, byte_storage_8_o5,
       byte_storage_8_o6, byte_storage_8_o7, byte_storage_8_o8, byte_storage_9_o1, byte_storage_9_o2,
       byte_storage_9_o3, byte_storage_9_o4, byte_storage_9_o5, byte_storage_9_o6, byte_storage_9_o7,
       byte_storage_9_o8, byte_storage_10_o1, byte_storage_10_o2, byte_storage_10_o3, byte_storage_10_o4,
       byte_storage_10_o5, byte_storage_10_o6, byte_storage_10_o7, byte_storage_10_o8, byte_storage_11_o1,
       byte_storage_11_o2, byte_storage_11_o3, byte_storage_11_o4, byte_storage_11_o5, byte_storage_11_o6,
       byte_storage_11_o7, byte_storage_11_o8, byte_storage_12_o1, byte_storage_12_o2, byte_storage_12_o3,
       byte_storage_12_o4, byte_storage_12_o5, byte_storage_12_o6, byte_storage_12_o7, byte_storage_12_o8,
       byte_storage_13_o1, byte_storage_13_o2, byte_storage_13_o3, byte_storage_13_o4, byte_storage_13_o5,
       byte_storage_13_o6, byte_storage_13_o7, byte_storage_13_o8, byte_storage_14_o1, byte_storage_14_o2,
       byte_storage_14_o3, byte_storage_14_o4, byte_storage_14_o5, byte_storage_14_o6, byte_storage_14_o7,
       byte_storage_14_o8, byte_storage_15_o1, byte_storage_15_o2, byte_storage_15_o3, byte_storage_15_o4,
       byte_storage_15_o5, byte_storage_15_o6, byte_storage_15_o7, byte_storage_15_o8, byte_storage_16_o1,
       byte_storage_16_o2, byte_storage_16_o3, byte_storage_16_o4, byte_storage_16_o5, byte_storage_16_o6,
       byte_storage_16_o7, byte_storage_16_o8, decoder_1_out0, decoder_1_out1, decoder_1_out2,
       decoder_1_out3, decoder_1_out4, decoder_1_out5, decoder_1_out6, decoder_1_out7, decoder_1_out8,
       decoder_1_out9, decoder_1_out10, decoder_1_out11, decoder_1_out12, decoder_1_out13, decoder_1_out14,
       decoder_1_out15, not_1_out, read_passing_2_o1, read_passing_2_o2, read_passing_2_o3,
       read_passing_2_o4, read_passing_2_o5, read_passing_2_o6, read_passing_2_o7, read_passing_2_o8,
       read_passing_3_o1, read_passing_3_o2, read_passing_3_o3, read_passing_3_o4, read_passing_3_o5,
       read_passing_3_o6, read_passing_3_o7, read_passing_3_o8, read_passing_4_o1, read_passing_4_o2,
       read_passing_4_o3, read_passing_4_o4, read_passing_4_o5, read_passing_4_o6, read_passing_4_o7,
       read_passing_4_o8, read_passing_5_o1, read_passing_5_o2, read_passing_5_o3, read_passing_5_o4,
       read_passing_5_o5, read_passing_5_o6, read_passing_5_o7, read_passing_5_o8, read_passing_6_o1,
       read_passing_6_o2, read_passing_6_o3, read_passing_6_o4, read_passing_6_o5, read_passing_6_o6,
       read_passing_6_o7, read_passing_6_o8, read_passing_7_o1, read_passing_7_o2, read_passing_7_o3,
       read_passing_7_o4, read_passing_7_o5, read_passing_7_o6, read_passing_7_o7, read_passing_7_o8,
       read_passing_8_o1, read_passing_8_o2, read_passing_8_o3, read_passing_8_o4, read_passing_8_o5,
       read_passing_8_o6, read_passing_8_o7, read_passing_8_o8, read_passing_9_o1, read_passing_9_o2,
       read_passing_9_o3, read_passing_9_o4, read_passing_9_o5, read_passing_9_o6, read_passing_9_o7,
       read_passing_9_o8, read_passing_10_o1, read_passing_10_o2, read_passing_10_o3, read_passing_10_o4,
       read_passing_10_o5, read_passing_10_o6, read_passing_10_o7, read_passing_10_o8, read_passing_11_o1,
       read_passing_11_o2, read_passing_11_o3, read_passing_11_o4, read_passing_11_o5, read_passing_11_o6,
       read_passing_11_o7, read_passing_11_o8, read_passing_12_o1, read_passing_12_o2, read_passing_12_o3,
       read_passing_12_o4, read_passing_12_o5, read_passing_12_o6, read_passing_12_o7, read_passing_12_o8,
       read_passing_13_o1, read_passing_13_o2, read_passing_13_o3, read_passing_13_o4, read_passing_13_o5,
       read_passing_13_o6, read_passing_13_o7, read_passing_13_o8, read_passing_14_o1, read_passing_14_o2,
       read_passing_14_o3, read_passing_14_o4, read_passing_14_o5, read_passing_14_o6, read_passing_14_o7,
       read_passing_14_o8, read_passing_15_o1, read_passing_15_o2, read_passing_15_o3, read_passing_15_o4,
       read_passing_15_o5, read_passing_15_o6, read_passing_15_o7, read_passing_15_o8, read_passing_16_o1,
       read_passing_16_o2, read_passing_16_o3, read_passing_16_o4, read_passing_16_o5, read_passing_16_o6,
       read_passing_16_o7, read_passing_16_o8;

  not not_1 (not_1_out, EnableWrite);
  byte_storage byte_storage_1 (
    .o2(byte_storage_1_o2), .o3(byte_storage_1_o3), .o1(byte_storage_1_o1), .b8(b8), .b7(b7), .b6(b6),
    .b5(b5), .b4(b4), .b3(b3), .b2(b2), .b1(b1), .Enable(and_1_out), .Clock(CLK), .o4(byte_storage_1_o4),
    .o5(byte_storage_1_o5), .o6(byte_storage_1_o6), .o7(byte_storage_1_o7), .o8(byte_storage_1_o8));
  and and_1 (and_1_out, not_1_out, decoder_1_out0);
  byte_storage byte_storage_2 (
    .o2(byte_storage_2_o2), .o3(byte_storage_2_o3), .o1(byte_storage_2_o1), .b8(b8), .b7(b7), .b6(b6),
    .b5(b5), .b4(b4), .b3(b3), .b2(b2), .b1(b1), .Enable(and_2_out), .Clock(CLK), .o4(byte_storage_2_o4),
    .o5(byte_storage_2_o5), .o6(byte_storage_2_o6), .o7(byte_storage_2_o7), .o8(byte_storage_2_o8));
  and and_2 (and_2_out, not_1_out, decoder_1_out1);
  byte_storage byte_storage_3 (
    .o2(byte_storage_3_o2), .o3(byte_storage_3_o3), .o1(byte_storage_3_o1), .b8(b8), .b7(b7), .b6(b6),
    .b5(b5), .b4(b4), .b3(b3), .b2(b2), .b1(b1), .Enable(and_3_out), .Clock(CLK), .o4(byte_storage_3_o4),
    .o5(byte_storage_3_o5), .o6(byte_storage_3_o6), .o7(byte_storage_3_o7), .o8(byte_storage_3_o8));
  and and_3 (and_3_out, not_1_out, decoder_1_out2);
  byte_storage byte_storage_4 (
    .o2(byte_storage_4_o2), .o3(byte_storage_4_o3), .o1(byte_storage_4_o1), .b8(b8), .b7(b7), .b6(b6),
    .b5(b5), .b4(b4), .b3(b3), .b2(b2), .b1(b1), .Enable(and_4_out), .Clock(CLK), .o4(byte_storage_4_o4),
    .o5(byte_storage_4_o5), .o6(byte_storage_4_o6), .o7(byte_storage_4_o7), .o8(byte_storage_4_o8));
  and and_4 (and_4_out, not_1_out, decoder_1_out3);
  byte_storage byte_storage_5 (
    .o2(byte_storage_5_o2), .o3(byte_storage_5_o3), .o1(byte_storage_5_o1), .b8(b8), .b7(b7), .b6(b6),
    .b5(b5), .b4(b4), .b3(b3), .b2(b2), .b1(b1), .Enable(and_5_out), .Clock(CLK), .o4(byte_storage_5_o4),
    .o5(byte_storage_5_o5), .o6(byte_storage_5_o6), .o7(byte_storage_5_o7), .o8(byte_storage_5_o8));
  and and_5 (and_5_out, not_1_out, decoder_1_out4);
  byte_storage byte_storage_6 (
    .o2(byte_storage_6_o2), .o3(byte_storage_6_o3), .o1(byte_storage_6_o1), .b8(b8), .b7(b7), .b6(b6),
    .b5(b5), .b4(b4), .b3(b3), .b2(b2), .b1(b1), .Enable(and_6_out), .Clock(CLK), .o4(byte_storage_6_o4),
    .o5(byte_storage_6_o5), .o6(byte_storage_6_o6), .o7(byte_storage_6_o7), .o8(byte_storage_6_o8));
  and and_6 (and_6_out, not_1_out, decoder_1_out5);
  byte_storage byte_storage_7 (
    .o2(byte_storage_7_o2), .o3(byte_storage_7_o3), .o1(byte_storage_7_o1), .b8(b8), .b7(b7), .b6(b6),
    .b5(b5), .b4(b4), .b3(b3), .b2(b2), .b1(b1), .Enable(and_7_out), .Clock(CLK), .o4(byte_storage_7_o4),
    .o5(byte_storage_7_o5), .o6(byte_storage_7_o6), .o7(byte_storage_7_o7), .o8(byte_storage_7_o8));
  and and_7 (and_7_out, not_1_out, decoder_1_out6);
  byte_storage byte_storage_8 (
    .o2(byte_storage_8_o2), .o3(byte_storage_8_o3), .o1(byte_storage_8_o1), .b8(b8), .b7(b7), .b6(b6),
    .b5(b5), .b4(b4), .b3(b3), .b2(b2), .b1(b1), .Enable(and_8_out), .Clock(CLK), .o4(byte_storage_8_o4),
    .o5(byte_storage_8_o5), .o6(byte_storage_8_o6), .o7(byte_storage_8_o7), .o8(byte_storage_8_o8));
  and and_8 (and_8_out, not_1_out, decoder_1_out7);
  byte_storage byte_storage_9 (
    .o2(byte_storage_9_o2), .o3(byte_storage_9_o3), .o1(byte_storage_9_o1), .b8(b8), .b7(b7), .b6(b6),
    .b5(b5), .b4(b4), .b3(b3), .b2(b2), .b1(b1), .Enable(and_9_out), .Clock(CLK), .o4(byte_storage_9_o4),
    .o5(byte_storage_9_o5), .o6(byte_storage_9_o6), .o7(byte_storage_9_o7), .o8(byte_storage_9_o8));
  and and_9 (and_9_out, not_1_out, decoder_1_out8);
  byte_storage byte_storage_10 (
    .o2(byte_storage_10_o2), .o3(byte_storage_10_o3), .o1(byte_storage_10_o1), .b8(b8), .b7(b7), .b6(b6),
    .b5(b5), .b4(b4), .b3(b3), .b2(b2), .b1(b1), .Enable(and_10_out), .Clock(CLK), .o4(byte_storage_10_o4),
    .o5(byte_storage_10_o5), .o6(byte_storage_10_o6), .o7(byte_storage_10_o7), .o8(byte_storage_10_o8));
  and and_10 (and_10_out, not_1_out, decoder_1_out9);
  byte_storage byte_storage_11 (
    .o2(byte_storage_11_o2), .o3(byte_storage_11_o3), .o1(byte_storage_11_o1), .b8(b8), .b7(b7), .b6(b6),
    .b5(b5), .b4(b4), .b3(b3), .b2(b2), .b1(b1), .Enable(and_11_out), .Clock(CLK), .o4(byte_storage_11_o4),
    .o5(byte_storage_11_o5), .o6(byte_storage_11_o6), .o7(byte_storage_11_o7), .o8(byte_storage_11_o8));
  and and_11 (and_11_out, not_1_out, decoder_1_out10);
  byte_storage byte_storage_12 (
    .o2(byte_storage_12_o2), .o3(byte_storage_12_o3), .o1(byte_storage_12_o1), .b8(b8), .b7(b7), .b6(b6),
    .b5(b5), .b4(b4), .b3(b3), .b2(b2), .b1(b1), .Enable(and_12_out), .Clock(CLK), .o4(byte_storage_12_o4),
    .o5(byte_storage_12_o5), .o6(byte_storage_12_o6), .o7(byte_storage_12_o7), .o8(byte_storage_12_o8));
  and and_12 (and_12_out, not_1_out, decoder_1_out11);
  byte_storage byte_storage_13 (
    .o2(byte_storage_13_o2), .o3(byte_storage_13_o3), .o1(byte_storage_13_o1), .b8(b8), .b7(b7), .b6(b6),
    .b5(b5), .b4(b4), .b3(b3), .b2(b2), .b1(b1), .Enable(and_13_out), .Clock(CLK), .o4(byte_storage_13_o4),
    .o5(byte_storage_13_o5), .o6(byte_storage_13_o6), .o7(byte_storage_13_o7), .o8(byte_storage_13_o8));
  and and_13 (and_13_out, not_1_out, decoder_1_out12);
  byte_storage byte_storage_14 (
    .o2(byte_storage_14_o2), .o3(byte_storage_14_o3), .o1(byte_storage_14_o1), .b8(b8), .b7(b7), .b6(b6),
    .b5(b5), .b4(b4), .b3(b3), .b2(b2), .b1(b1), .Enable(and_14_out), .Clock(CLK), .o4(byte_storage_14_o4),
    .o5(byte_storage_14_o5), .o6(byte_storage_14_o6), .o7(byte_storage_14_o7), .o8(byte_storage_14_o8));
  and and_14 (and_14_out, not_1_out, decoder_1_out13);
  byte_storage byte_storage_15 (
    .o2(byte_storage_15_o2), .o3(byte_storage_15_o3), .o1(byte_storage_15_o1), .b8(b8), .b7(b7), .b6(b6),
    .b5(b5), .b4(b4), .b3(b3), .b2(b2), .b1(b1), .Enable(and_15_out), .Clock(CLK), .o4(byte_storage_15_o4),
    .o5(byte_storage_15_o5), .o6(byte_storage_15_o6), .o7(byte_storage_15_o7), .o8(byte_storage_15_o8));
  and and_15 (and_15_out, not_1_out, decoder_1_out14);
  byte_storage byte_storage_16 (
    .o2(byte_storage_16_o2), .o3(byte_storage_16_o3), .o1(byte_storage_16_o1), .b8(b8), .b7(b7), .b6(b6),
    .b5(b5), .b4(b4), .b3(b3), .b2(b2), .b1(b1), .Enable(and_16_out), .Clock(CLK), .o4(byte_storage_16_o4),
    .o5(byte_storage_16_o5), .o6(byte_storage_16_o6), .o7(byte_storage_16_o7), .o8(byte_storage_16_o8));
  and and_16 (and_16_out, not_1_out, decoder_1_out15);
  Decoder #(.select(4), .enable("false")) decoder_1 (
    .out0(decoder_1_out0), .out1(decoder_1_out1), .out2(decoder_1_out2), .out3(decoder_1_out3),
    .out4(decoder_1_out4), .out5(decoder_1_out5), .out6(decoder_1_out6), .out7(decoder_1_out7),
    .out8(decoder_1_out8), .out9(decoder_1_out9), .out10(decoder_1_out10), .out11(decoder_1_out11),
    .out12(decoder_1_out12), .out13(decoder_1_out13), .out14(decoder_1_out14), .out15(decoder_1_out15),
    .sel({addr4, addr3, addr2, addr1}));
  read_passing read_passing_1 (
    .o1(o1), .b8(read_passing_2_o8), .b7(read_passing_2_o7), .b6(read_passing_2_o6), .b5(read_passing_2_o5),
    .b4(read_passing_2_o4), .b3(read_passing_2_o3), .b2(read_passing_2_o2), .b1(read_passing_2_o1),
    .n8(byte_storage_1_o8), .n7(byte_storage_1_o7), .n6(byte_storage_1_o6), .n5(byte_storage_1_o5),
    .n4(byte_storage_1_o4), .n3(byte_storage_1_o3), .n2(byte_storage_1_o2), .n1(byte_storage_1_o1),
    .Enable(decoder_1_out0), .o2(o2), .o3(o3), .o4(o4), .o5(o5), .o6(o6), .o7(o7), .o8(o8));
  read_passing read_passing_2 (
    .o1(read_passing_2_o1), .b8(read_passing_3_o8), .b7(read_passing_3_o7), .b6(read_passing_3_o6),
    .b5(read_passing_3_o5), .b4(read_passing_3_o4), .b3(read_passing_3_o3), .b2(read_passing_3_o2),
    .b1(read_passing_3_o1), .n8(byte_storage_2_o8), .n7(byte_storage_2_o7), .n6(byte_storage_2_o6),
    .n5(byte_storage_2_o5), .n4(byte_storage_2_o4), .n3(byte_storage_2_o3), .n2(byte_storage_2_o2),
    .n1(byte_storage_2_o1), .Enable(decoder_1_out1), .o2(read_passing_2_o2), .o3(read_passing_2_o3),
    .o4(read_passing_2_o4), .o5(read_passing_2_o5), .o6(read_passing_2_o6), .o7(read_passing_2_o7),
    .o8(read_passing_2_o8));
  read_passing read_passing_3 (
    .o1(read_passing_3_o1), .b8(read_passing_4_o8), .b7(read_passing_4_o7), .b6(read_passing_4_o6),
    .b5(read_passing_4_o5), .b4(read_passing_4_o4), .b3(read_passing_4_o3), .b2(read_passing_4_o2),
    .b1(read_passing_4_o1), .n8(byte_storage_3_o8), .n7(byte_storage_3_o7), .n6(byte_storage_3_o6),
    .n5(byte_storage_3_o5), .n4(byte_storage_3_o4), .n3(byte_storage_3_o3), .n2(byte_storage_3_o2),
    .n1(byte_storage_3_o1), .Enable(decoder_1_out2), .o2(read_passing_3_o2), .o3(read_passing_3_o3),
    .o4(read_passing_3_o4), .o5(read_passing_3_o5), .o6(read_passing_3_o6), .o7(read_passing_3_o7),
    .o8(read_passing_3_o8));
  read_passing read_passing_4 (
    .o1(read_passing_4_o1), .b8(read_passing_5_o8), .b7(read_passing_5_o7), .b6(read_passing_5_o6),
    .b5(read_passing_5_o5), .b4(read_passing_5_o4), .b3(read_passing_5_o3), .b2(read_passing_5_o2),
    .b1(read_passing_5_o1), .n8(byte_storage_4_o8), .n7(byte_storage_4_o7), .n6(byte_storage_4_o6),
    .n5(byte_storage_4_o5), .n4(byte_storage_4_o4), .n3(byte_storage_4_o3), .n2(byte_storage_4_o2),
    .n1(byte_storage_4_o1), .Enable(decoder_1_out3), .o2(read_passing_4_o2), .o3(read_passing_4_o3),
    .o4(read_passing_4_o4), .o5(read_passing_4_o5), .o6(read_passing_4_o6), .o7(read_passing_4_o7),
    .o8(read_passing_4_o8));
  read_passing read_passing_5 (
    .o1(read_passing_5_o1), .b8(read_passing_6_o8), .b7(read_passing_6_o7), .b6(read_passing_6_o6),
    .b5(read_passing_6_o5), .b4(read_passing_6_o4), .b3(read_passing_6_o3), .b2(read_passing_6_o2),
    .b1(read_passing_6_o1), .n8(byte_storage_5_o8), .n7(byte_storage_5_o7), .n6(byte_storage_5_o6),
    .n5(byte_storage_5_o5), .n4(byte_storage_5_o4), .n3(byte_storage_5_o3), .n2(byte_storage_5_o2),
    .n1(byte_storage_5_o1), .Enable(decoder_1_out4), .o2(read_passing_5_o2), .o3(read_passing_5_o3),
    .o4(read_passing_5_o4), .o5(read_passing_5_o5), .o6(read_passing_5_o6), .o7(read_passing_5_o7),
    .o8(read_passing_5_o8));
  read_passing read_passing_6 (
    .o1(read_passing_6_o1), .b8(read_passing_7_o8), .b7(read_passing_7_o7), .b6(read_passing_7_o6),
    .b5(read_passing_7_o5), .b4(read_passing_7_o4), .b3(read_passing_7_o3), .b2(read_passing_7_o2),
    .b1(read_passing_7_o1), .n8(byte_storage_6_o8), .n7(byte_storage_6_o7), .n6(byte_storage_6_o6),
    .n5(byte_storage_6_o5), .n4(byte_storage_6_o4), .n3(byte_storage_6_o3), .n2(byte_storage_6_o2),
    .n1(byte_storage_6_o1), .Enable(decoder_1_out5), .o2(read_passing_6_o2), .o3(read_passing_6_o3),
    .o4(read_passing_6_o4), .o5(read_passing_6_o5), .o6(read_passing_6_o6), .o7(read_passing_6_o7),
    .o8(read_passing_6_o8));
  read_passing read_passing_7 (
    .o1(read_passing_7_o1), .b8(read_passing_8_o8), .b7(read_passing_8_o7), .b6(read_passing_8_o6),
    .b5(read_passing_8_o5), .b4(read_passing_8_o4), .b3(read_passing_8_o3), .b2(read_passing_8_o2),
    .b1(read_passing_8_o1), .n8(byte_storage_7_o8), .n7(byte_storage_7_o7), .n6(byte_storage_7_o6),
    .n5(byte_storage_7_o5), .n4(byte_storage_7_o4), .n3(byte_storage_7_o3), .n2(byte_storage_7_o2),
    .n1(byte_storage_7_o1), .Enable(decoder_1_out6), .o2(read_passing_7_o2), .o3(read_passing_7_o3),
    .o4(read_passing_7_o4), .o5(read_passing_7_o5), .o6(read_passing_7_o6), .o7(read_passing_7_o7),
    .o8(read_passing_7_o8));
  read_passing read_passing_8 (
    .o1(read_passing_8_o1), .b8(read_passing_9_o8), .b7(read_passing_9_o7), .b6(read_passing_9_o6),
    .b5(read_passing_9_o5), .b4(read_passing_9_o4), .b3(read_passing_9_o3), .b2(read_passing_9_o2),
    .b1(read_passing_9_o1), .n8(byte_storage_8_o8), .n7(byte_storage_8_o7), .n6(byte_storage_8_o6),
    .n5(byte_storage_8_o5), .n4(byte_storage_8_o4), .n3(byte_storage_8_o3), .n2(byte_storage_8_o2),
    .n1(byte_storage_8_o1), .Enable(decoder_1_out7), .o2(read_passing_8_o2), .o3(read_passing_8_o3),
    .o4(read_passing_8_o4), .o5(read_passing_8_o5), .o6(read_passing_8_o6), .o7(read_passing_8_o7),
    .o8(read_passing_8_o8));
  read_passing read_passing_9 (
    .o1(read_passing_9_o1), .b8(read_passing_10_o8), .b7(read_passing_10_o7), .b6(read_passing_10_o6),
    .b5(read_passing_10_o5), .b4(read_passing_10_o4), .b3(read_passing_10_o3), .b2(read_passing_10_o2),
    .b1(read_passing_10_o1), .n8(byte_storage_9_o8), .n7(byte_storage_9_o7), .n6(byte_storage_9_o6),
    .n5(byte_storage_9_o5), .n4(byte_storage_9_o4), .n3(byte_storage_9_o3), .n2(byte_storage_9_o2),
    .n1(byte_storage_9_o1), .Enable(decoder_1_out8), .o2(read_passing_9_o2), .o3(read_passing_9_o3),
    .o4(read_passing_9_o4), .o5(read_passing_9_o5), .o6(read_passing_9_o6), .o7(read_passing_9_o7),
    .o8(read_passing_9_o8));
  read_passing read_passing_10 (
    .o1(read_passing_10_o1), .b8(read_passing_11_o8), .b7(read_passing_11_o7), .b6(read_passing_11_o6),
    .b5(read_passing_11_o5), .b4(read_passing_11_o4), .b3(read_passing_11_o3), .b2(read_passing_11_o2),
    .b1(read_passing_11_o1), .n8(byte_storage_10_o8), .n7(byte_storage_10_o7), .n6(byte_storage_10_o6),
    .n5(byte_storage_10_o5), .n4(byte_storage_10_o4), .n3(byte_storage_10_o3), .n2(byte_storage_10_o2),
    .n1(byte_storage_10_o1), .Enable(decoder_1_out9), .o2(read_passing_10_o2), .o3(read_passing_10_o3),
    .o4(read_passing_10_o4), .o5(read_passing_10_o5), .o6(read_passing_10_o6), .o7(read_passing_10_o7),
    .o8(read_passing_10_o8));
  read_passing read_passing_11 (
    .o1(read_passing_11_o1), .b8(read_passing_12_o8), .b7(read_passing_12_o7), .b6(read_passing_12_o6),
    .b5(read_passing_12_o5), .b4(read_passing_12_o4), .b3(read_passing_12_o3), .b2(read_passing_12_o2),
    .b1(read_passing_12_o1), .n8(byte_storage_11_o8), .n7(byte_storage_11_o7), .n6(byte_storage_11_o6),
    .n5(byte_storage_11_o5), .n4(byte_storage_11_o4), .n3(byte_storage_11_o3), .n2(byte_storage_11_o2),
    .n1(byte_storage_11_o1), .Enable(decoder_1_out10), .o2(read_passing_11_o2), .o3(read_passing_11_o3),
    .o4(read_passing_11_o4), .o5(read_passing_11_o5), .o6(read_passing_11_o6), .o7(read_passing_11_o7),
    .o8(read_passing_11_o8));
  read_passing read_passing_12 (
    .o1(read_passing_12_o1), .b8(read_passing_13_o8), .b7(read_passing_13_o7), .b6(read_passing_13_o6),
    .b5(read_passing_13_o5), .b4(read_passing_13_o4), .b3(read_passing_13_o3), .b2(read_passing_13_o2),
    .b1(read_passing_13_o1), .n8(byte_storage_12_o8), .n7(byte_storage_12_o7), .n6(byte_storage_12_o6),
    .n5(byte_storage_12_o5), .n4(byte_storage_12_o4), .n3(byte_storage_12_o3), .n2(byte_storage_12_o2),
    .n1(byte_storage_12_o1), .Enable(decoder_1_out11), .o2(read_passing_12_o2), .o3(read_passing_12_o3),
    .o4(read_passing_12_o4), .o5(read_passing_12_o5), .o6(read_passing_12_o6), .o7(read_passing_12_o7),
    .o8(read_passing_12_o8));
  read_passing read_passing_13 (
    .o1(read_passing_13_o1), .b8(read_passing_14_o8), .b7(read_passing_14_o7), .b6(read_passing_14_o6),
    .b5(read_passing_14_o5), .b4(read_passing_14_o4), .b3(read_passing_14_o3), .b2(read_passing_14_o2),
    .b1(read_passing_14_o1), .n8(byte_storage_13_o8), .n7(byte_storage_13_o7), .n6(byte_storage_13_o6),
    .n5(byte_storage_13_o5), .n4(byte_storage_13_o4), .n3(byte_storage_13_o3), .n2(byte_storage_13_o2),
    .n1(byte_storage_13_o1), .Enable(decoder_1_out12), .o2(read_passing_13_o2), .o3(read_passing_13_o3),
    .o4(read_passing_13_o4), .o5(read_passing_13_o5), .o6(read_passing_13_o6), .o7(read_passing_13_o7),
    .o8(read_passing_13_o8));
  read_passing read_passing_14 (
    .o1(read_passing_14_o1), .b8(read_passing_15_o8), .b7(read_passing_15_o7), .b6(read_passing_15_o6),
    .b5(read_passing_15_o5), .b4(read_passing_15_o4), .b3(read_passing_15_o3), .b2(read_passing_15_o2),
    .b1(read_passing_15_o1), .n8(byte_storage_14_o8), .n7(byte_storage_14_o7), .n6(byte_storage_14_o6),
    .n5(byte_storage_14_o5), .n4(byte_storage_14_o4), .n3(byte_storage_14_o3), .n2(byte_storage_14_o2),
    .n1(byte_storage_14_o1), .Enable(decoder_1_out13), .o2(read_passing_14_o2), .o3(read_passing_14_o3),
    .o4(read_passing_14_o4), .o5(read_passing_14_o5), .o6(read_passing_14_o6), .o7(read_passing_14_o7),
    .o8(read_passing_14_o8));
  read_passing read_passing_15 (
    .o1(read_passing_15_o1), .b8(read_passing_16_o8), .b7(read_passing_16_o7), .b6(read_passing_16_o6),
    .b5(read_passing_16_o5), .b4(read_passing_16_o4), .b3(read_passing_16_o3), .b2(read_passing_16_o2),
    .b1(read_passing_16_o1), .n8(byte_storage_15_o8), .n7(byte_storage_15_o7), .n6(byte_storage_15_o6),
    .n5(byte_storage_15_o5), .n4(byte_storage_15_o4), .n3(byte_storage_15_o3), .n2(byte_storage_15_o2),
    .n1(byte_storage_15_o1), .Enable(decoder_1_out14), .o2(read_passing_15_o2), .o3(read_passing_15_o3),
    .o4(read_passing_15_o4), .o5(read_passing_15_o5), .o6(read_passing_15_o6), .o7(read_passing_15_o7),
    .o8(read_passing_15_o8));
  read_passing read_passing_16 (
    .o1(read_passing_16_o1), .n8(byte_storage_16_o8), .n7(byte_storage_16_o7), .n6(byte_storage_16_o6),
    .n5(byte_storage_16_o5), .n4(byte_storage_16_o4), .n3(byte_storage_16_o3), .n2(byte_storage_16_o2),
    .n1(byte_storage_16_o1), .Enable(decoder_1_out15), .o2(read_passing_16_o2), .o3(read_passing_16_o3),
    .o4(read_passing_16_o4), .o5(read_passing_16_o5), .o6(read_passing_16_o6), .o7(read_passing_16_o7),
    .o8(read_passing_16_o8));  // open: b8, b7, b6, b5, b4, b3, b2, b1
endmodule

module byte_storage (
  input  Clock,
  input  Enable,
  input  b1,
  input  b2,
  input  b3,
  input  b4,
  input  b5,
  input  b6,
  input  b7,
  input  b8,
  output o1,
  output o2,
  output o3,
  output o4,
  output o5,
  output o6,
  output o7,
  output o8
);

  wire and_1_out, and_2_out, and_3_out, and_4_out, and_5_out, and_6_out, and_7_out, and_8_out, and_9_out,
       and_10_out, and_11_out, and_12_out, and_13_out, and_14_out, and_15_out, and_16_out;

  and and_1 (and_1_out, Enable, b1);
  J_K_Flip_Flop j_k_ff_1 (.J(and_1_out), .K(and_2_out), .clk(Clock), .Q(o1));  // open: Qn, preset, reset
  and and_2 (and_2_out, Enable, ~b1);  // AND_Gate
  J_K_Flip_Flop j_k_ff_2 (.J(and_3_out), .K(and_4_out), .clk(Clock), .Q(o2));  // open: Qn, preset, reset
  and and_3 (and_3_out, Enable, b2);
  and and_4 (and_4_out, Enable, ~b2);  // AND_Gate
  and and_5 (and_5_out, Enable, b3);
  J_K_Flip_Flop j_k_ff_3 (.J(and_5_out), .K(and_6_out), .clk(Clock), .Q(o3));  // open: Qn, preset, reset
  and and_6 (and_6_out, Enable, ~b3);  // AND_Gate
  and and_7 (and_7_out, Enable, b4);
  J_K_Flip_Flop j_k_ff_4 (.J(and_7_out), .K(and_8_out), .clk(Clock), .Q(o4));  // open: Qn, preset, reset
  and and_8 (and_8_out, Enable, ~b4);  // AND_Gate
  J_K_Flip_Flop j_k_ff_5 (.J(and_9_out), .K(and_10_out), .clk(Clock), .Q(o5));  // open: Qn, preset, reset
  and and_9 (and_9_out, Enable, b5);
  and and_10 (and_10_out, Enable, ~b5);  // AND_Gate
  and and_11 (and_11_out, Enable, b6);
  J_K_Flip_Flop j_k_ff_6 (.J(and_11_out), .K(and_12_out), .clk(Clock), .Q(o6));  // open: Qn, preset, reset
  and and_12 (and_12_out, Enable, ~b6);  // AND_Gate
  and and_13 (and_13_out, Enable, b7);
  J_K_Flip_Flop j_k_ff_7 (.J(and_13_out), .K(and_14_out), .clk(Clock), .Q(o7));  // open: Qn, preset, reset
  and and_14 (and_14_out, Enable, ~b7);  // AND_Gate
  J_K_Flip_Flop j_k_ff_8 (.J(and_15_out), .K(and_16_out), .clk(Clock), .Q(o8));  // open: Qn, preset, reset
  and and_15 (and_15_out, Enable, b8);
  and and_16 (and_16_out, Enable, ~b8);  // AND_Gate
endmodule

module read_passing (
  input  Enable,
  input  n1,
  input  n2,
  input  n3,
  input  n4,
  input  n5,
  input  n6,
  input  n7,
  input  n8,
  input  b1,
  input  b2,
  input  b3,
  input  b4,
  input  b5,
  input  b6,
  input  b7,
  input  b8,
  output o1,
  output o2,
  output o3,
  output o4,
  output o5,
  output o6,
  output o7,
  output o8
);

  wire and_1_out, and_2_out, and_3_out, and_4_out, and_5_out, and_6_out, and_7_out, and_8_out;

  and and_1 (and_1_out, n1, Enable);
  or or_1 (o1, and_1_out, b1);
  and and_2 (and_2_out, n2, Enable);
  or or_2 (o2, and_2_out, b2);
  and and_3 (and_3_out, n3, Enable);
  and and_4 (and_4_out, n4, Enable);
  and and_5 (and_5_out, n5, Enable);
  and and_6 (and_6_out, n6, Enable);
  and and_7 (and_7_out, n7, Enable);
  and and_8 (and_8_out, n8, Enable);
  or or_3 (o3, and_3_out, b3);
  or or_4 (o4, and_4_out, b4);
  or or_5 (o5, and_5_out, b5);
  or or_6 (o6, and_6_out, b6);
  or or_7 (o7, and_7_out, b7);
  or or_8 (o8, and_8_out, b8);
endmodule

module ALU (
  input  [7:0] in_1,
  input  in_2,
  input  [7:0] in_3,
  output [7:0] A_Register,
  output [2:0] status
);

  wire clock_1_out;
  wire [2:0] add_8bit_1_status_overflow_negative_zero;
  wire [7:0] add_8bit_1_sum, Left_Register_out1, Right_Register_out1;

  Clock clock_1 (.out(clock_1_out));
  Register8Bit Right_Register (.in1(in_3), .out1(Right_Register_out1), .Enbl(clock_1_out));
  Register8Bit Left_Register (.in1(in_1), .out1(Left_Register_out1), .Enbl(clock_1_out));
  Add_8bit add_8bit_1 (
    .B(Right_Register_out1), .A(Left_Register_out1), .Add_Sub(in_2), .Sum(add_8bit_1_sum),
    .Status_Overflow_Negative_Zero(add_8bit_1_status_overflow_negative_zero));
  Register8Bit register8bit_1 (.in1(add_8bit_1_sum), .out1(A_Register), .Enbl(clock_1_out));
  Register3Bit register3bit_1 (.in1(add_8bit_1_status_overflow_negative_zero), .in_2(clock_1_out), .out1(status));
endmodule

module numeric_keypad (
  input  D0,
  input  D1,
  input  D2,
  input  D3,
  input  D4,
  input  D5,
  input  D6,
  input  D7,
  input  D8,
  input  D9,
  output [7:0] out_11
);

  wire clock_1_out, or_1_out, or_2_out, or_3_out, or_4_out;

  or or_1 (or_1_out, D8, D9);
  or or_2 (or_2_out, D4, D5, D7, D7);
  or or_3 (or_3_out, D6, D3, D2, D7);
  or or_4 (or_4_out, D9, D7, D5, D3, D1);
  Multiplexer #(.enable("false")) multiplexer_1 (.in0(1'b0), .in1(or_1_out), .out(out_11[3]), .sel(clock_1_out));
  Clock clock_1 (.out(clock_1_out));
  Multiplexer #(.enable("false")) multiplexer_2 (.in0(1'b0), .in1(or_2_out), .out(out_11[2]), .sel(clock_1_out));
  Multiplexer #(.enable("false")) multiplexer_3 (.in0(1'b0), .in1(or_3_out), .out(out_11[1]), .sel(clock_1_out));
  Multiplexer #(.enable("false")) multiplexer_4 (.in0(1'b0), .in1(or_4_out), .out(out_11[0]), .sel(clock_1_out));

  assign out_11[7:4] = 4'b0000;
endmodule

module Add_1Bit (
  input  A,
  input  B,
  input  Cin,
  output Sum,
  output Cout
);

  wire and_1_out, and_2_out, xor_1_out;

  xor xor_1 (xor_1_out, A, B);
  and and_1 (and_1_out, xor_1_out, Cin);
  and and_2 (and_2_out, A, B);
  xor xor_2 (Sum, xor_1_out, Cin);
  or or_1 (Cout, and_1_out, and_2_out);
endmodule

module MAR (
  input  [3:0] In1,
  input  [3:0] Out1
);

  wire clock_1_out;

  Clock clock_1 (.out(clock_1_out));
  D_Flip_Flop d_ff_1 (.D(In1[0]), .clk(clock_1_out), .Q(Out1[0]));  // open: Qn, preset, reset
  D_Flip_Flop d_ff_2 (.D(In1[1]), .clk(clock_1_out), .Q(Out1[1]));  // open: Qn, preset, reset
  D_Flip_Flop d_ff_3 (.D(In1[2]), .clk(clock_1_out), .Q(Out1[2]));  // open: Qn, preset, reset
  D_Flip_Flop d_ff_4 (.D(In1[3]), .clk(clock_1_out), .Q(Out1[3]));  // open: Qn, preset, reset
endmodule

module BCDComponent (
  input  in_1,
  input  in_2,
  input  in_3,
  input  in_4,
  input  [3:0] in_5,
  output out_6,
  output out_7,
  output out_8,
  output out_9,
  output [3:0] out_10
);

  wire and_2_out, and_3_out, and_5_out, and_6_out, and_7_out, and_8_out, and_10_out, and_12_out, and_13_out,
       and_14_out, and_15_out, not_1_out, not_2_out, or_1_out, or_2_out, or_3_out, or_4_out, or_5_out,
       RetZero_out, xor_1_out;

  or or_1 (or_1_out, in_1, and_5_out);
  and and_1 (out_6, or_1_out, not_2_out);
  and and_2 (and_2_out, in_1, ~in_2, ~in_3, in_4);  // AND_Gate
  and and_3 (and_3_out, in_2, ~in_3, ~in_4);  // AND_Gate
  or or_2 (or_2_out, and_2_out, and_3_out);
  and and_4 (out_7, or_2_out, not_2_out);
  or or_3 (or_3_out, in_3, in_4);
  and and_5 (and_5_out, in_2, or_3_out);
  and and_6 (and_6_out, in_1, ~in_2, ~in_3, ~in_4);  // AND_Gate
  and and_7 (and_7_out, ~in_1, in_2, in_3, ~in_4);  // AND_Gate
  or or_4 (or_4_out, in_3, and_6_out);
  and and_8 (and_8_out, or_4_out, ~and_7_out);  // AND_Gate
  and and_9 (out_8, and_8_out, not_2_out);
  and and_10 (and_10_out, ~in_1, in_2, ~in_4, not_1_out);  // AND_Gate
  xor xor_1 (xor_1_out, and_10_out, or_5_out);
  and and_11 (out_9, xor_1_out, not_2_out);
  and and_12 (and_12_out, in_1, ~in_2, ~in_4);  // AND_Gate
  and and_13 (and_13_out, ~in_1, in_2, ~in_3, ~in_4);  // AND_Gate
  not not_1 (not_1_out, and_13_out);
  and and_14 (and_14_out, ~in_2, ~in_3);  // AND_Gate
  and and_15 (and_15_out, ~in_1, ~in_2, in_4);  // AND_Gate
  and RetZero (RetZero_out, in_1, ~and_14_out);  // AND_Gate
  not not_2 (not_2_out, RetZero_out);
  or or_5 (or_5_out, and_12_out, and_15_out);
endmodule

module BCD (
  input  in_1,
  input  in_2,
  input  in_3,
  input  in_4,
  input  in_5,
  input  in_6,
  input  in_7,
  input  in_8,
  output out_9,
  output out_10,
  output out_11,
  output out_12,
  output out_13,
  output out_14,
  output out_15,
  output out_16,
  output out_17,
  output out_18
);

  wire bcdcomponent_1_out_6, bcdcomponent_1_out_7, bcdcomponent_1_out_8, bcdcomponent_1_out_9,
       bcdcomponent_2_out_7, bcdcomponent_2_out_8, bcdcomponent_2_out_9, bcdcomponent_4_out_6,
       bcdcomponent_4_out_7, bcdcomponent_4_out_8, bcdcomponent_4_out_9, bcdcomponent_5_out_6,
       bcdcomponent_5_out_7, bcdcomponent_5_out_8, bcdcomponent_5_out_9, bcdcomponent_6_out_6,
       bcdcomponent_6_out_7, bcdcomponent_6_out_8, bcdcomponent_6_out_9;

  BCDComponent bcdcomponent_1 (
    .out_7(bcdcomponent_1_out_7), .out_8(bcdcomponent_1_out_8), .out_6(bcdcomponent_1_out_6), .in_4(in_3),
    .in_3(in_2), .in_2(in_1), .out_9(bcdcomponent_1_out_9));  // open: in_1, in_5, out_10
  BCDComponent bcdcomponent_2 (
    .out_7(bcdcomponent_2_out_7), .out_8(bcdcomponent_2_out_8), .out_6(out_9), .in_4(bcdcomponent_5_out_6),
    .in_3(bcdcomponent_4_out_6), .in_2(bcdcomponent_1_out_6), .out_9(bcdcomponent_2_out_9));  // open: in_1, in_5, out_10
  BCDComponent bcdcomponent_3 (
    .out_7(out_11), .out_8(out_12), .out_6(out_10), .in_4(bcdcomponent_6_out_6), .in_3(bcdcomponent_2_out_9),
    .in_2(bcdcomponent_2_out_8), .in_1(bcdcomponent_2_out_7), .out_9(out_13));  // open: in_5, out_10
  BCDComponent bcdcomponent_4 (
    .out_7(bcdcomponent_4_out_7), .out_8(bcdcomponent_4_out_8), .out_6(bcdcomponent_4_out_6), .in_4(in_4),
    .in_3(bcdcomponent_1_out_9), .in_2(bcdcomponent_1_out_8), .in_1(bcdcomponent_1_out_7),
    .out_9(bcdcomponent_4_out_9));  // open: in_5, out_10
  BCDComponent bcdcomponent_5 (
    .out_7(bcdcomponent_5_out_7), .out_8(bcdcomponent_5_out_8), .out_6(bcdcomponent_5_out_6), .in_4(in_5),
    .in_3(bcdcomponent_4_out_9), .in_2(bcdcomponent_4_out_8), .in_1(bcdcomponent_4_out_7),
    .out_9(bcdcomponent_5_out_9));  // open: in_5, out_10
  BCDComponent bcdcomponent_6 (
    .out_7(bcdcomponent_6_out_7), .out_8(bcdcomponent_6_out_8), .out_6(bcdcomponent_6_out_6), .in_4(in_6),
    .in_3(bcdcomponent_5_out_9), .in_2(bcdcomponent_5_out_8), .in_1(bcdcomponent_5_out_7),
    .out_9(bcdcomponent_6_out_9));  // open: in_5, out_10
  BCDComponent bcdcomponent_7 (
    .out_7(out_15), .out_8(out_16), .out_6(out_14), .in_4(in_7), .in_3(bcdcomponent_6_out_9),
    .in_2(bcdcomponent_6_out_8), .in_1(bcdcomponent_6_out_7), .out_9(out_17));  // open: in_5, out_10

  assign out_18 = in_8;
endmodule

module digit (
  input  in_1,
  input  in_2,
  input  in_3,
  input  in_4,
  output out_5,
  output out_6,
  output out_7,
  output out_8,
  output out_9,
  output out_10,
  output out_11
);

  wire and_1_out, and_2_out, and_3_out, and_4_out, and_5_out, and_6_out, and_7_out, and_8_out, and_9_out,
       and_10_out, and_11_out, xnor_1_out, xor_1_out;

  and and_1 (and_1_out, ~in_1, ~in_2);  // AND_Gate
  and and_2 (and_2_out, ~in_1, ~in_2, ~in_3);  // AND_Gate
  and and_3 (and_3_out, ~in_1, ~in_2, ~in_3, ~in_4);  // AND_Gate
  and and_4 (and_4_out, in_2, in_3, in_4);
  and and_5 (and_5_out, in_2, ~in_3, ~in_4);  // AND_Gate
  and and_6 (and_6_out, and_1_out, ~and_3_out);  // AND_Gate
  xor xor_1 (xor_1_out, in_4, in_3);
  and and_7 (and_7_out, in_2, ~in_3);  // AND_Gate
  and and_8 (and_8_out, in_3, in_4);
  and and_9 (and_9_out, ~in_2, ~in_3, in_4);  // AND_Gate
  nor nor_1 (out_5, and_2_out, and_4_out);
  nor nor_2 (out_6, and_6_out, and_4_out);
  nand nand_1 (out_8, in_2, xor_1_out);
  and and_10 (and_10_out, ~in_1, ~in_2, ~in_3, in_4);  // AND_Gate
  xnor xnor_1 (xnor_1_out, in_3, in_4);
  and and_11 (and_11_out, xnor_1_out, in_2);
  nor nor_3 (out_7, and_5_out, and_10_out);
  nand nand_2 (out_11, ~in_1, ~in_2, in_3, ~in_4);  // NAND_Gate
  nor nor_4 (out_10, and_10_out, and_11_out);
  nor nor_5 (out_9, and_7_out, and_8_out, and_9_out);
endmodule

module PC_incr (
  input  [3:0] PCIn,
  output [3:0] PCOut
);

  Add_4bit add_4bit_1 (.B(4'b0001), .A(PCIn), .Sum(PCOut));  // open: in_3, out_5
endmodule

module Add_8bit (
  input  [7:0] B,
  input  [7:0] A,
  input  Add_Sub,
  output [7:0] Sum,
  output [2:0] Status_Overflow_Negative_Zero
);

  wire add_1bit_1_cout, add_1bit_2_cout, add_1bit_3_cout, add_1bit_4_cout, add_1bit_5_cout, add_1bit_6_cout,
       add_1bit_7_cout, add_1bit_8_cout, or_1_out, or_2_out, or_3_out, or_4_out, or_5_out, or_6_out,
       or_7_out, or_8_out;

  or or_1 (or_1_out, B[0], Add_Sub);
  or or_2 (or_2_out, B[1], Add_Sub);
  or or_3 (or_3_out, B[2], Add_Sub);
  or or_4 (or_4_out, B[3], Add_Sub);
  or or_5 (or_5_out, B[4], Add_Sub);
  or or_6 (or_6_out, B[5], Add_Sub);
  or or_7 (or_7_out, B[6], Add_Sub);
  or or_8 (or_8_out, B[7], Add_Sub);
  Add_1Bit add_1bit_1 (.A(A[0]), .B(or_1_out), .Cin(1'b0), .Sum(Sum[0]), .Cout(add_1bit_1_cout));
  Add_1Bit add_1bit_2 (.A(A[1]), .B(or_2_out), .Cin(add_1bit_1_cout), .Sum(Sum[1]), .Cout(add_1bit_2_cout));
  Add_1Bit add_1bit_3 (.A(A[2]), .B(or_3_out), .Cin(add_1bit_2_cout), .Sum(Sum[2]), .Cout(add_1bit_3_cout));
  Add_1Bit add_1bit_4 (.A(A[3]), .B(or_4_out), .Cin(add_1bit_3_cout), .Sum(Sum[3]), .Cout(add_1bit_4_cout));
  Add_1Bit add_1bit_5 (.A(A[4]), .B(or_5_out), .Cin(add_1bit_4_cout), .Sum(Sum[4]), .Cout(add_1bit_5_cout));
  Add_1Bit add_1bit_6 (.A(A[5]), .B(or_6_out), .Cin(add_1bit_5_cout), .Sum(Sum[5]), .Cout(add_1bit_6_cout));
  Add_1Bit add_1bit_7 (.A(A[6]), .B(or_7_out), .Cin(add_1bit_6_cout), .Sum(Sum[6]), .Cout(add_1bit_7_cout));
  Add_1Bit add_1bit_8 (
    .A(A[7]), .B(or_8_out), .Cin(add_1bit_7_cout), .Sum(Status_Overflow_Negative_Zero[1]),
    .Cout(add_1bit_8_cout));
  and and_1 (Status_Overflow_Negative_Zero[2], ~Sum[0], ~Sum[1], ~Sum[2], ~Sum[3], ~Sum[4], ~Sum[5], ~Sum[6], ~Status_Overflow_Negative_Zero[1]);  // AND_Gate
  or or_9 (Status_Overflow_Negative_Zero[0], add_1bit_7_cout, add_1bit_8_cout);

  assign Sum[7] = Status_Overflow_Negative_Zero[1];
endmodule

module Register8Bit (
  input  [7:0] in1,
  input  Enbl,
  output [7:0] out1
);

  D_Flip_Flop d_ff_1 (.D(in1[0]), .clk(Enbl), .Q(out1[0]));  // open: Qn, preset, reset
  D_Flip_Flop d_ff_2 (.D(in1[1]), .clk(Enbl), .Q(out1[1]));  // open: Qn, preset, reset
  D_Flip_Flop d_ff_3 (.D(in1[2]), .clk(Enbl), .Q(out1[2]));  // open: Qn, preset, reset
  D_Flip_Flop d_ff_4 (.D(in1[3]), .clk(Enbl), .Q(out1[3]));  // open: Qn, preset, reset
  D_Flip_Flop d_ff_5 (.D(in1[4]), .clk(Enbl), .Q(out1[4]));  // open: Qn, preset, reset
  D_Flip_Flop d_ff_6 (.D(in1[5]), .clk(Enbl), .Q(out1[5]));  // open: Qn, preset, reset
  D_Flip_Flop d_ff_7 (.D(in1[6]), .clk(Enbl), .Q(out1[6]));  // open: Qn, preset, reset
  D_Flip_Flop d_ff_8 (.D(in1[7]), .clk(Enbl), .Q(out1[7]));  // open: Qn, preset, reset
endmodule

module Register3Bit (
  input  [2:0] in1,
  input  in_2,
  output [2:0] out1
);

  D_Flip_Flop d_ff_1 (.D(in1[0]), .clk(in_2), .Q(out1[0]));  // open: Qn, preset, reset
  D_Flip_Flop d_ff_2 (.D(in1[1]), .clk(in_2), .Q(out1[1]));  // open: Qn, preset, reset
  D_Flip_Flop d_ff_3 (.D(in1[2]), .clk(in_2), .Q(out1[2]));  // open: Qn, preset, reset
endmodule

module sysBus (
  input  [7:0] in_1,
  input  [7:0] in_2,
  input  in_3,
  output [7:0] out_4
);

  Multiplexer #(.width(8), .enable("false")) multiplexer_1 (.in0(in_1), .in1(in_2), .out(out_4), .sel(in_3));
endmodule

module Add_4bit (
  input  [3:0] B,
  input  [3:0] A,
  input  in_3,
  output [3:0] Sum,
  output out_5
);

  wire add_1bit_1_cout, add_1bit_2_cout, add_1bit_3_cout;

  Add_1Bit add_1bit_1 (.A(A[0]), .B(B[0]), .Cin(in_3), .Sum(Sum[0]), .Cout(add_1bit_1_cout));
  Add_1Bit add_1bit_2 (.A(A[1]), .B(B[1]), .Cin(add_1bit_1_cout), .Sum(Sum[1]), .Cout(add_1bit_2_cout));
  Add_1Bit add_1bit_3 (.A(A[2]), .B(B[2]), .Cin(add_1bit_2_cout), .Sum(Sum[2]), .Cout(add_1bit_3_cout));
  Add_1Bit add_1bit_4 (.A(A[3]), .B(B[3]), .Cin(add_1bit_3_cout), .Sum(Sum[3]), .Cout(out_5));
endmodule

module Mult (
  input  [3:0] in_1,
  input  [3:0] in_2
);

  wire [3:0] add_4bit_1_sum, add_4bit_2_sum, and_2_out, and_4_out, and_9_out, and_13_out;
  wire [5:0] undriven, undriven_2;

  and and_1 (and_2_out[1], in_1[1], in_1[2]);
  and and_2 (and_2_out[0], in_1[1], in_1[3]);
  and and_3 (and_2_out[2], in_1[1], in_1[1]);
  Add_4bit add_4bit_1 (.B(and_4_out), .A(and_2_out), .Sum(add_4bit_1_sum));  // open: in_3, out_5
  and and_4 (and_4_out[0], in_2[2], in_1[3]);
  and and_5 (and_2_out[3], in_1[1], in_1[0]);
  and and_6 (and_4_out[1], in_2[2], in_1[2]);
  and and_7 (and_4_out[2], in_2[2], in_1[1]);
  and and_8 (and_4_out[3], in_2[2], in_1[0]);
  Add_6bit add_6bit_1 (
    .in_1({undriven[5], add_4bit_1_sum, undriven[0]}), .in_2(undriven_2));  // open: in_3, out_4, out_5
  and and_9 (and_9_out[0], in_2[1], in_1[3]);
  and and_10 (and_9_out[1], in_2[1], in_1[2]);
  and and_11 (and_9_out[2], in_2[1], in_1[1]);
  Add_4bit add_4bit_2 (.B(and_13_out), .A(and_9_out), .Sum(add_4bit_2_sum));  // open: in_3, out_5
  and and_12 (and_9_out[3], in_2[1], in_1[0]);
  and and_13 (and_13_out[0], in_1[0], in_1[3]);
  and and_14 (and_13_out[1], in_1[0], in_1[2]);
  and and_15 (and_13_out[2], in_1[0], in_1[1]);
  and and_16 (and_13_out[3], in_1[0], in_1[0]);

  assign {in_2[3], in_2[0]} = in_1[1:0];
endmodule

module Add_6bit (
  input  [5:0] in_1,
  input  [5:0] in_2,
  input  in_3,
  output [5:0] out_4,
  output out_5
);

  wire add_1bit_1_cout, add_1bit_2_cout, add_1bit_3_cout, add_1bit_4_cout, add_1bit_5_cout;

  Add_1Bit add_1bit_1 (.A(in_2[0]), .B(in_1[0]), .Cin(in_3), .Sum(out_4[0]), .Cout(add_1bit_1_cout));
  Add_1Bit add_1bit_2 (.A(in_2[1]), .B(in_1[1]), .Cin(add_1bit_1_cout), .Sum(out_4[1]), .Cout(add_1bit_2_cout));
  Add_1Bit add_1bit_3 (.A(in_2[2]), .B(in_1[2]), .Cin(add_1bit_2_cout), .Sum(out_4[2]), .Cout(add_1bit_3_cout));
  Add_1Bit add_1bit_4 (.A(in_2[3]), .B(in_1[3]), .Cin(add_1bit_3_cout), .Sum(out_4[3]), .Cout(add_1bit_4_cout));
  Add_1Bit add_1bit_5 (.A(in_2[4]), .B(in_1[4]), .Cin(add_1bit_4_cout), .Sum(out_4[4]), .Cout(add_1bit_5_cout));
  Add_1Bit add_1bit_6 (.A(in_2[5]), .B(in_1[5]), .Cin(add_1bit_5_cout), .Sum(out_4[5]), .Cout(out_5));
endmodule
