// Logisim project Display.circ as structural Verilog: 5 circuits, main circuit display_data
module display_data (
  input  [7:0] in_1,
  input  Error,
  input  Reset,
  output out_4,
  output out_5,
  output out_6,
  output out_7,
  output out_8,
  output out_9,
  output out_10,
  output out_11,
  output out_12,
  output out_13,
  output out_14,
  output out_15,
  output out_16,
  output out_17,
  output out_18,
  output out_19,
  output out_20,
  output out_21,
  output out_22,
  output out_23,
  output out_24
);

  wire bcd_1_out_2, bcd_1_out_3, bcd_1_out_4, bcd_1_out_5, bcd_1_out_6, bcd_1_out_7, bcd_1_out_8,
       bcd_1_out_9, bcd_1_out_10, bcd_1_out_11;

  // Probe on in_1
  BCD bcd_1 (
    .in_1(in_1), .out_2(bcd_1_out_2), .out_3(bcd_1_out_3), .out_4(bcd_1_out_4), .out_5(bcd_1_out_5),
    .out_6(bcd_1_out_6), .out_7(bcd_1_out_7), .out_8(bcd_1_out_8), .out_9(bcd_1_out_9),
    .out_10(bcd_1_out_10), .out_11(bcd_1_out_11));
  digit digit_1 (
    .in_3(bcd_1_out_2), .in_4(bcd_1_out_3), .Error(Error), .Reset(Reset),
    .out_7({out_5, out_6, out_7, out_4, out_8, out_9, out_10}));  // open: in_1, in_2
  digit digit_2 (
    .in_1(bcd_1_out_4), .in_2(bcd_1_out_5), .in_3(bcd_1_out_6), .in_4(bcd_1_out_7), .Error(Error),
    .Reset(Reset), .out_7({out_12, out_13, out_14, out_11, out_15, out_16, out_17}));
  digit digit_3 (
    .in_1(bcd_1_out_8), .in_2(bcd_1_out_9), .in_3(bcd_1_out_10), .in_4(bcd_1_out_11), .Error(Error),
    .Reset(Reset), .out_7({out_19, out_20, out_21, out_18, out_22, out_23, out_24}));
endmodule

module BCD_component (
  input  in_1,
  input  in_2,
  input  in_3,
  input  in_4,
  output out_5,
  output out_6,
  output out_7,
  output out_8
);

  wire and_2_out, and_3_out, and_5_out, and_6_out, and_7_out, and_8_out, and_10_out, and_12_out, and_13_out,
       and_14_out, and_15_out, not_1_out, not_2_out, or_1_out, or_2_out, or_3_out, or_4_out, or_5_out,
       RetZero_out, xor_1_out;

  or or_1 (or_1_out, in_1, and_5_out);
  and and_1 (out_5, or_1_out, not_2_out);
  and and_2 (and_2_out, in_2, ~in_3, ~in_4);  // AND_Gate
  and and_3 (and_3_out, in_1, ~in_2, ~in_3, in_4);  // AND_Gate
  or or_2 (or_2_out, and_3_out, and_2_out);
  and and_4 (out_6, or_2_out, not_2_out);
  or or_3 (or_3_out, in_3, in_4);
  and and_5 (and_5_out, in_2, or_3_out);
  and and_6 (and_6_out, ~in_1, in_2, in_3, ~in_4);  // AND_Gate
  and and_7 (and_7_out, in_1, ~in_2, ~in_3, ~in_4);  // AND_Gate
  or or_4 (or_4_out, in_3, and_7_out);
  and and_8 (and_8_out, or_4_out, ~and_6_out);  // AND_Gate
  and and_9 (out_7, and_8_out, not_2_out);
  and and_10 (and_10_out, ~in_1, in_2, ~in_4, not_1_out);  // AND_Gate
  xor xor_1 (xor_1_out, and_10_out, or_5_out);
  and and_11 (out_8, xor_1_out, not_2_out);
  and and_12 (and_12_out, ~in_1, in_2, ~in_3, ~in_4);  // AND_Gate
  and and_13 (and_13_out, in_1, ~in_2, ~in_4);  // AND_Gate
  not not_1 (not_1_out, and_12_out);
  and and_14 (and_14_out, ~in_2, ~in_3);  // AND_Gate
  and and_15 (and_15_out, ~in_1, ~in_2, in_4);  // AND_Gate
  and RetZero (RetZero_out, in_1, ~and_14_out);  // AND_Gate
  not not_2 (not_2_out, RetZero_out);
  or or_5 (or_5_out, and_13_out, and_15_out);
endmodule

module BCD (
  input  [7:0] in_1,
  output out_2,
  output out_3,
  output out_4,
  output out_5,
  output out_6,
  output out_7,
  output out_8,
  output out_9,
  output out_10,
  output out_11
);

  wire bcd_component_1_out_5, bcd_component_1_out_6, bcd_component_1_out_7, bcd_component_1_out_8,
       bcd_component_2_out_5, bcd_component_2_out_6, bcd_component_2_out_7, bcd_component_2_out_8,
       bcd_component_3_out_5, bcd_component_3_out_6, bcd_component_3_out_7, bcd_component_3_out_8,
       bcd_component_4_out_6, bcd_component_4_out_7, bcd_component_4_out_8, bcd_component_6_out_5,
       bcd_component_6_out_6, bcd_component_6_out_7, bcd_component_6_out_8;

  // Probe on in_1
  BCD_component bcd_component_1 (
    .out_7(bcd_component_1_out_7), .out_6(bcd_component_1_out_6), .out_5(bcd_component_1_out_5),
    .in_4(in_1[5]), .in_3(in_1[6]), .in_2(in_1[7]), .out_8(bcd_component_1_out_8));  // open: in_1
  BCD_component bcd_component_2 (
    .out_7(bcd_component_2_out_7), .out_6(bcd_component_2_out_6), .out_5(bcd_component_2_out_5),
    .in_4(in_1[4]), .in_3(bcd_component_1_out_8), .in_2(bcd_component_1_out_7), .in_1(bcd_component_1_out_6),
    .out_8(bcd_component_2_out_8));
  BCD_component bcd_component_3 (
    .out_7(bcd_component_3_out_7), .out_6(bcd_component_3_out_6), .out_5(bcd_component_3_out_5),
    .in_4(in_1[3]), .in_3(bcd_component_2_out_8), .in_2(bcd_component_2_out_7), .in_1(bcd_component_2_out_6),
    .out_8(bcd_component_3_out_8));
  BCD_component bcd_component_4 (
    .out_7(bcd_component_4_out_7), .out_6(bcd_component_4_out_6), .out_5(out_2),
    .in_4(bcd_component_3_out_5), .in_3(bcd_component_2_out_5), .in_2(bcd_component_1_out_5),
    .out_8(bcd_component_4_out_8));  // open: in_1
  BCD_component bcd_component_5 (
    .out_7(out_5), .out_6(out_4), .out_5(out_3), .in_4(bcd_component_6_out_5), .in_3(bcd_component_4_out_8),
    .in_2(bcd_component_4_out_7), .in_1(bcd_component_4_out_6), .out_8(out_6));
  BCD_component bcd_component_6 (
    .out_7(bcd_component_6_out_7), .out_6(bcd_component_6_out_6), .out_5(bcd_component_6_out_5),
    .in_4(in_1[2]), .in_3(bcd_component_3_out_8), .in_2(bcd_component_3_out_7), .in_1(bcd_component_3_out_6),
    .out_8(bcd_component_6_out_8));
  BCD_component bcd_component_7 (
    .out_7(out_9), .out_6(out_8), .out_5(out_7), .in_4(in_1[1]), .in_3(bcd_component_6_out_8),
    .in_2(bcd_component_6_out_7), .in_1(bcd_component_6_out_6), .out_8(out_10));
  // Probe on {out_2, out_3}
  // Probe on {out_4, out_5, out_6, out_7}
  // Probe on {out_8, out_9, out_10, in_1[0]}

  assign out_11 = in_1[0];
endmodule

module digit (
  input  in_1,
  input  in_2,
  input  in_3,
  input  in_4,
  input  Error,
  input  Reset,
  output [6:0] out_7
);

  wire [6:0] multiplexer_1_out;

  Multiplexer #(.select(4), .width(7), .enable("false")) multiplexer_1 (
    .in0(7'b1110111), .in1(7'b0010001), .in2(7'b0111110), .in3(7'b0111011), .in4(7'b1011001),
    .in5(7'b1101011), .in6(7'b1101111), .in7(7'b1110001), .in8({7{1'b1}}), .in9(7'b1111011),
    .out(multiplexer_1_out), .sel({in_1, in_2, in_3, in_4}));  // open: in10, in11, in12, in13, in14, in15
  Multiplexer #(.select(2), .width(7), .enable("false")) multiplexer_2 (
    .in0(multiplexer_1_out), .in1(7'b1101110), .in2({7{1'b0}}), .in3({7{1'b0}}), .out(out_7),
    .sel({Reset, Error}));
endmodule

module display_test (
  input  [7:0] in_1,
  input  in_2,
  input  in_3
);

  wire display_data_1_out_4, display_data_1_out_5, display_data_1_out_6, display_data_1_out_7,
       display_data_1_out_8, display_data_1_out_9, display_data_1_out_10, display_data_1_out_11,
       display_data_1_out_12, display_data_1_out_13, display_data_1_out_14, display_data_1_out_15,
       display_data_1_out_16, display_data_1_out_17, display_data_1_out_18, display_data_1_out_19,
       display_data_1_out_20, display_data_1_out_21, display_data_1_out_22, display_data_1_out_23,
       display_data_1_out_24;

  // Probe on in_1
  _7_Segment_Display u_7_segment_display_1 (
    .g(display_data_1_out_4), .f(display_data_1_out_5), .a(display_data_1_out_6), .b(display_data_1_out_7),
    .e(display_data_1_out_8), .d(display_data_1_out_9), .c(display_data_1_out_10));  // open: dp
  _7_Segment_Display u_7_segment_display_2 (
    .g(display_data_1_out_18), .f(display_data_1_out_19), .a(display_data_1_out_20),
    .b(display_data_1_out_21), .e(display_data_1_out_22), .d(display_data_1_out_23), .c(display_data_1_out_24));  // open: dp
  _7_Segment_Display u_7_segment_display_3 (
    .g(display_data_1_out_11), .f(display_data_1_out_12), .a(display_data_1_out_13),
    .b(display_data_1_out_14), .e(display_data_1_out_15), .d(display_data_1_out_16), .c(display_data_1_out_17));  // open: dp
  display_data display_data_1 (
    .out_17(display_data_1_out_17), .out_16(display_data_1_out_16), .out_15(display_data_1_out_15),
    .out_14(display_data_1_out_14), .out_13(display_data_1_out_13), .out_12(display_data_1_out_12),
    .out_11(display_data_1_out_11), .out_10(display_data_1_out_10), .out_9(display_data_1_out_9),
    .out_8(display_data_1_out_8), .out_7(display_data_1_out_7), .out_6(display_data_1_out_6),
    .out_5(display_data_1_out_5), .out_4(display_data_1_out_4), .Reset(in_3), .Error(in_2), .in_1(in_1),
    .out_18(display_data_1_out_18), .out_19(display_data_1_out_19), .out_20(display_data_1_out_20),
    .out_21(display_data_1_out_21), .out_22(display_data_1_out_22), .out_23(display_data_1_out_23),
    .out_24(display_data_1_out_24));
endmodule
