// Logisim project Four_Bits_Add_Sub.circ as structural Verilog: 4 circuits, main circuit Add_Sub_4Bits
module Add_Sub_4Bits (
  input  [7:0] A,
  input  [7:0] B,
  input  Add_Sub,
  output [2:0] Zero_Neg_Over,
  output [7:0] R
);

  wire add_1bit_1_cout, add_1bit_2_cout, add_1bit_3_cout, add_1bit_4_cout, add_1bit_5_cout, add_1bit_6_cout,
       add_1bit_7_cout, not_1_out, twos_comp_1_aout, twos_comp_1_bout, twos_comp_1_cout, twos_comp_1_dout,
       twos_comp_1_out_14, twos_comp_1_out_15, twos_comp_1_out_16, twos_comp_1_out_17, twos_comp_1_overflow;

  not not_1 (not_1_out, Add_Sub);
  Twos_Comp twos_comp_1 (
    .Enable(not_1_out), .A(B[0]), .B(B[1]), .C(B[2]), .D(B[3]), .in_6(B[4]), .in_7(B[5]), .in_8(B[6]),
    .in_9(B[7]), .Aout(twos_comp_1_aout), .Bout(twos_comp_1_bout), .Cout(twos_comp_1_cout),
    .Dout(twos_comp_1_dout), .out_14(twos_comp_1_out_14), .out_15(twos_comp_1_out_15),
    .out_16(twos_comp_1_out_16), .out_17(twos_comp_1_out_17), .Overflow(twos_comp_1_overflow));
  Add_1Bit add_1bit_1 (.Sum(R[0]), .A(twos_comp_1_aout), .B(A[0]), .Cout(add_1bit_1_cout));  // open: Cin
  Add_1Bit add_1bit_2 (.Sum(R[1]), .A(twos_comp_1_bout), .B(A[1]), .Cout(add_1bit_2_cout), .Cin(add_1bit_1_cout));
  Add_1Bit add_1bit_3 (.Sum(R[2]), .A(twos_comp_1_cout), .B(A[2]), .Cout(add_1bit_3_cout), .Cin(add_1bit_2_cout));
  Add_1Bit add_1bit_4 (.Sum(R[3]), .A(twos_comp_1_dout), .B(A[3]), .Cout(add_1bit_4_cout), .Cin(add_1bit_3_cout));
  Add_1Bit add_1bit_5 (.Sum(R[4]), .A(twos_comp_1_out_14), .B(A[4]), .Cout(add_1bit_5_cout), .Cin(add_1bit_4_cout));
  Add_1Bit add_1bit_6 (.Sum(R[5]), .A(twos_comp_1_out_15), .B(A[5]), .Cout(add_1bit_6_cout), .Cin(add_1bit_5_cout));
  Add_1Bit add_1bit_7 (.Sum(R[6]), .A(twos_comp_1_out_16), .B(A[6]), .Cout(add_1bit_7_cout), .Cin(add_1bit_6_cout));
  Add_1Bit add_1bit_8 (.Sum(R[7]), .A(twos_comp_1_out_17), .B(A[7]), .Cin(add_1bit_7_cout));  // open: Cout
  and and_1 (Zero_Neg_Over[1], R[7], Zero_Neg_Over[2]);
  and and_2 (Zero_Neg_Over[0], ~R[0], ~R[1], ~R[2], ~R[3], ~R[4], ~R[5], ~R[6], ~R[7], ~Zero_Neg_Over[2]);  // AND_Gate
  Overfloww overfloww_1 (.Ain(A[7]), .Bin(twos_comp_1_overflow), .Rout(R[7]), .Overflow(Zero_Neg_Over[2]));

  // Notes on the sheet:
  //   Allan Wang - 260667681
endmodule

module Add_1Bit (
  input  Cin,
  input  A,
  input  B,
  output Sum,
  output Cout
);

  wire and_1_out, and_2_out, and_3_out, and_4_out, and_5_out, not_1_out, or_1_out;

  and and_1 (and_1_out, Cin, A, B);
  or or_1 (or_1_out, Cin, A, B);
  not not_1 (not_1_out, Cout);
  and and_2 (and_2_out, A, B);
  and and_3 (and_3_out, A, Cin);
  and and_4 (and_4_out, B, Cin);
  and and_5 (and_5_out, or_1_out, not_1_out);
  or or_2 (Cout, and_2_out, and_3_out, and_4_out);
  or or_3 (Sum, and_1_out, and_5_out);

  // Notes on the sheet:
  //   YOUR NAME AND STUDENT NUMBER HERE
endmodule

module Twos_Comp (
  input  Enable,
  input  A,
  input  B,
  input  C,
  input  D,
  input  in_6,
  input  in_7,
  input  in_8,
  input  in_9,
  output Aout,
  output Bout,
  output Cout,
  output Dout,
  output out_14,
  output out_15,
  output out_16,
  output out_17,
  output Overflow
);

  wire add_1bit_1_cout, add_1bit_1_sum, add_1bit_2_cout, add_1bit_2_sum, add_1bit_3_cout, add_1bit_3_sum,
       add_1bit_4_cout, add_1bit_4_sum, add_1bit_5_cout, add_1bit_5_sum, add_1bit_6_sum, add_1bit_7_sum,
       add_1bit_8_cout, add_1bit_8_sum, and_1_out, and_2_out, and_3_out, and_4_out, and_5_out, and_6_out,
       and_7_out, and_8_out, and_9_out, and_10_out, and_11_out, and_12_out, and_13_out, and_14_out,
       and_15_out, and_16_out, not_1_out, not_2_out, not_3_out, not_4_out, not_5_out, not_6_out, not_7_out,
       not_8_out;

  not not_1 (not_1_out, in_8);
  not not_2 (not_2_out, in_9);
  not not_3 (not_3_out, A);
  not not_4 (not_4_out, B);
  not not_5 (not_5_out, C);
  not not_6 (not_6_out, D);
  not not_7 (not_7_out, in_6);
  not not_8 (not_8_out, in_7);
  and and_1 (and_1_out, Enable, add_1bit_1_sum);
  Add_1Bit add_1bit_1 (.Sum(add_1bit_1_sum), .A(not_3_out), .Cout(add_1bit_1_cout), .Cin(Enable));  // open: B
  and and_2 (and_2_out, ~Enable, A);  // AND_Gate
  and and_3 (and_3_out, Enable, add_1bit_2_sum);
  Add_1Bit add_1bit_2 (.Sum(add_1bit_2_sum), .A(not_4_out), .Cout(add_1bit_2_cout), .Cin(add_1bit_1_cout));  // open: B
  and and_4 (and_4_out, ~Enable, B);  // AND_Gate
  and and_5 (and_5_out, Enable, add_1bit_3_sum);
  Add_1Bit add_1bit_3 (.Sum(add_1bit_3_sum), .A(not_5_out), .Cout(add_1bit_3_cout), .Cin(add_1bit_2_cout));  // open: B
  and and_6 (and_6_out, ~Enable, C);  // AND_Gate
  and and_7 (and_7_out, Enable, add_1bit_4_sum);
  Add_1Bit add_1bit_4 (.Sum(add_1bit_4_sum), .A(not_6_out), .Cout(add_1bit_4_cout), .Cin(add_1bit_3_cout));  // open: B
  and and_8 (and_8_out, ~Enable, D);  // AND_Gate
  and and_9 (and_9_out, Enable, add_1bit_5_sum);
  Add_1Bit add_1bit_5 (.Sum(add_1bit_5_sum), .A(not_7_out), .Cout(add_1bit_5_cout), .Cin(add_1bit_4_cout));  // open: B
  and and_10 (and_10_out, ~Enable, in_6);  // AND_Gate
  and and_11 (and_11_out, Enable, add_1bit_6_sum);
  Add_1Bit add_1bit_6 (.Sum(add_1bit_6_sum), .A(not_8_out), .Cin(add_1bit_5_cout));  // open: B, Cout
  and and_12 (and_12_out, ~Enable, in_7);  // AND_Gate
  and and_13 (and_13_out, Enable, add_1bit_7_sum);
  Add_1Bit add_1bit_7 (.Sum(add_1bit_7_sum), .A(not_1_out));  // open: B, Cout, Cin
  and and_14 (and_14_out, ~Enable, in_8);  // AND_Gate
  and and_15 (and_15_out, Enable, add_1bit_8_sum);
  Add_1Bit add_1bit_8 (.Sum(add_1bit_8_sum), .A(not_2_out), .Cout(add_1bit_8_cout));  // open: B, Cin
  and and_16 (and_16_out, ~Enable, in_9);  // AND_Gate
  and and_17 (Overflow, add_1bit_8_cout, Enable);
  or or_1 (Aout, and_1_out, and_2_out);
  or or_2 (Bout, and_3_out, and_4_out);
  or or_3 (Cout, and_5_out, and_6_out);
  or or_4 (Dout, and_7_out, and_8_out);
  or or_5 (out_14, and_9_out, and_10_out);
  or or_6 (out_15, and_11_out, and_12_out);
  or or_7 (out_16, and_13_out, and_14_out);
  or or_8 (out_17, and_15_out, and_16_out);
endmodule

module Overfloww (
  input  Ain,
  input  Bin,
  input  Rout,
  output Overflow
);

  wire and_1_out, and_2_out;

  and and_1 (and_1_out, Ain, Bin, ~Rout);  // AND_Gate
  and and_2 (and_2_out, ~Ain, ~Bin, Rout);  // AND_Gate
  or or_1 (Overflow, and_1_out, and_2_out);

  // Notes on the sheet:
  //   Overflows occure when + and + -> - or - and - -> +
endmodule
