// Logisim project Memory16.circ as structural Verilog: 5 circuits, main circuit byte_storage_compact
module byte_storage_compact (
  input  Clock,
  input  EnableWrite,
  input  [7:0] datain,
  output [7:0] dataout
);

  wire and_1_out, and_2_out, and_3_out, and_4_out, and_5_out, and_6_out, and_7_out, and_8_out, and_9_out,
       and_10_out, and_11_out, and_12_out, and_13_out, and_14_out, and_15_out, and_16_out;

  and and_1 (and_1_out, EnableWrite, datain[0]);
  J_K_Flip_Flop j_k_ff_1 (.J(and_1_out), .K(and_2_out), .clk(Clock), .Q(dataout[0]));  // open: Qn, preset, reset
  and and_2 (and_2_out, EnableWrite, ~datain[0]);  // AND_Gate
  and and_3 (and_3_out, EnableWrite, datain[1]);
  J_K_Flip_Flop j_k_ff_2 (.J(and_3_out), .K(and_4_out), .clk(Clock), .Q(dataout[1]));  // open: Qn, preset, reset
  and and_4 (and_4_out, EnableWrite, ~datain[1]);  // AND_Gate
  J_K_Flip_Flop j_k_ff_3 (.J(and_5_out), .K(and_6_out), .clk(Clock), .Q(dataout[2]));  // open: Qn, preset, reset
  and and_5 (and_5_out, EnableWrite, datain[2]);
  and and_6 (and_6_out, EnableWrite, ~datain[2]);  // AND_Gate
  J_K_Flip_Flop j_k_ff_4 (.J(and_7_out), .K(and_8_out), .clk(Clock), .Q(dataout[3]));  // open: Qn, preset, reset
  and and_7 (and_7_out, EnableWrite, datain[3]);
  and and_8 (and_8_out, EnableWrite, ~datain[3]);  // AND_Gate
  J_K_Flip_Flop j_k_ff_5 (.J(and_9_out), .K(and_10_out), .clk(Clock), .Q(dataout[4]));  // open: Qn, preset, reset
  and and_9 (and_9_out, EnableWrite, datain[4]);
  and and_10 (and_10_out, EnableWrite, ~datain[4]);  // AND_Gate
  J_K_Flip_Flop j_k_ff_6 (.J(and_11_out), .K(and_12_out), .clk(Clock), .Q(dataout[5]));  // open: Qn, preset, reset
  and and_11 (and_11_out, EnableWrite, datain[5]);
  and and_12 (and_12_out, EnableWrite, ~datain[5]);  // AND_Gate
  J_K_Flip_Flop j_k_ff_7 (.J(and_13_out), .K(and_14_out), .clk(Clock), .Q(dataout[6]));  // open: Qn, preset, reset
  and and_13 (and_13_out, EnableWrite, datain[6]);
  and and_14 (and_14_out, EnableWrite, ~datain[6]);  // AND_Gate
  J_K_Flip_Flop j_k_ff_8 (.J(and_15_out), .K(and_16_out), .clk(Clock), .Q(dataout[7]));  // open: Qn, preset, reset
  and and_15 (and_15_out, EnableWrite, datain[7]);
  and and_16 (and_16_out, EnableWrite, ~datain[7]);  // AND_Gate
endmodule

module RAM16C (
  input  [3:0] Addr,
  input  EnableWrite,
  input  CLK,
  input  [7:0] DataInput,
  input  ROMoverwrite,
  input  Reset,
  input  [7:0] in_7,
  input  [7:0] in_8,
  input  [7:0] in_9,
  input  [7:0] in_10,
  input  [7:0] in_11,
  input  [7:0] in_12,
  input  [7:0] in_13,
  input  [7:0] in_14,
  input  [7:0] in_15,
  input  [7:0] in_16,
  input  [7:0] in_17,
  input  [7:0] in_18,
  input  [7:0] in_19,
  input  [7:0] in_20,
  input  [7:0] in_21,
  input  [7:0] in_22,
  output [7:0] out_23,
  output [7:0] out_24,
  output [7:0] out_25,
  output [7:0] out_26,
  output [7:0] out_27,
  output [7:0] out_28,
  output [7:0] out_29,
  output [7:0] out_30,
  output [7:0] out_31,
  output [7:0] out_32,
  output [7:0] out_33,
  output [7:0] out_34,
  output [7:0] out_35,
  output [7:0] out_36,
  output [7:0] out_37,
  output [7:0] out_38,
  output [7:0] out_39
);

  wire and_1_out, and_2_out, and_3_out, and_4_out, and_5_out, and_6_out, and_7_out, and_8_out, and_9_out,
       and_10_out, and_11_out, and_12_out, and_13_out, and_14_out, and_15_out, and_16_out, decoder_1_out0,
       decoder_1_out1, decoder_1_out2, decoder_1_out3, decoder_1_out4, decoder_1_out5, decoder_1_out6,
       decoder_1_out7, decoder_1_out8, decoder_1_out9, decoder_1_out10, decoder_1_out11, decoder_1_out12,
       decoder_1_out13, decoder_1_out14, decoder_1_out15, or_1_out, or_2_out, or_3_out, or_4_out, or_5_out,
       or_6_out, or_7_out, or_8_out, or_9_out, or_10_out, or_11_out, or_12_out, or_13_out, or_14_out,
       or_15_out, or_16_out;
  wire [7:0] multiplexer_1_out, multiplexer_2_out, multiplexer_3_out, multiplexer_4_out, multiplexer_5_out,
       multiplexer_6_out, multiplexer_7_out, multiplexer_8_out, multiplexer_9_out, multiplexer_10_out,
       multiplexer_11_out, multiplexer_12_out, multiplexer_13_out, multiplexer_14_out, multiplexer_15_out,
       multiplexer_16_out;

  or or_1 (or_1_out, ROMoverwrite, Reset, and_1_out);
  or or_2 (or_2_out, ROMoverwrite, Reset, and_2_out);
  or or_3 (or_3_out, ROMoverwrite, Reset, and_3_out);
  or or_4 (or_4_out, ROMoverwrite, Reset, and_4_out);
  or or_5 (or_5_out, ROMoverwrite, Reset, and_5_out);
  or or_6 (or_6_out, ROMoverwrite, Reset, and_6_out);
  or or_7 (or_7_out, ROMoverwrite, Reset, and_7_out);
  or or_8 (or_8_out, ROMoverwrite, Reset, and_8_out);
  or or_9 (or_9_out, ROMoverwrite, Reset, and_9_out);
  or or_10 (or_10_out, ROMoverwrite, Reset, and_10_out);
  or or_11 (or_11_out, ROMoverwrite, Reset, and_11_out);
  or or_12 (or_12_out, ROMoverwrite, Reset, and_12_out);
  or or_13 (or_13_out, ROMoverwrite, Reset, and_13_out);
  or or_14 (or_14_out, ROMoverwrite, Reset, and_14_out);
  or or_15 (or_15_out, ROMoverwrite, Reset, and_15_out);
  or or_16 (or_16_out, ROMoverwrite, Reset, and_16_out);
  Multiplexer #(.select(2), .width(8), .enable("false")) multiplexer_1 (
    .in0(DataInput), .in1(in_7), .in2({8{1'b0}}), .in3({8{1'b0}}), .out(multiplexer_1_out),
    .sel({Reset, ROMoverwrite}));
  and and_1 (and_1_out, EnableWrite, decoder_1_out0);
  Multiplexer #(.select(2), .width(8), .enable("false")) multiplexer_2 (
    .in0(DataInput), .in1(in_8), .in2({8{1'b0}}), .in3({8{1'b0}}), .out(multiplexer_2_out),
    .sel({Reset, ROMoverwrite}));
  and and_2 (and_2_out, EnableWrite, decoder_1_out1);
  Multiplexer #(.select(2), .width(8), .enable("false")) multiplexer_3 (
    .in0(DataInput), .in1(in_9), .in2({8{1'b0}}), .in3({8{1'b0}}), .out(multiplexer_3_out),
    .sel({Reset, ROMoverwrite}));
  and and_3 (and_3_out, EnableWrite, decoder_1_out2);
  Multiplexer #(.select(2), .width(8), .enable("false")) multiplexer_4 (
    .in0(DataInput), .in1(in_10), .in2({8{1'b0}}), .in3({8{1'b0}}), .out(multiplexer_4_out),
    .sel({Reset, ROMoverwrite}));
  and and_4 (and_4_out, EnableWrite, decoder_1_out3);
  Multiplexer #(.select(2), .width(8), .enable("false")) multiplexer_5 (
    .in0(DataInput), .in1(in_11), .in2({8{1'b0}}), .in3({8{1'b0}}), .out(multiplexer_5_out),
    .sel({Reset, ROMoverwrite}));
  and and_5 (and_5_out, EnableWrite, decoder_1_out4);
  Multiplexer #(.select(2), .width(8), .enable("false")) multiplexer_6 (
    .in0(DataInput), .in1(in_12), .in2({8{1'b0}}), .in3({8{1'b0}}), .out(multiplexer_6_out),
    .sel({Reset, ROMoverwrite}));
  and and_6 (and_6_out, EnableWrite, decoder_1_out5);
  Multiplexer #(.select(2), .width(8), .enable("false")) multiplexer_7 (
    .in0(DataInput), .in1(in_13), .in2({8{1'b0}}), .in3({8{1'b0}}), .out(multiplexer_7_out),
    .sel({Reset, ROMoverwrite}));
  and and_7 (and_7_out, EnableWrite, decoder_1_out6);
  Multiplexer #(.select(2), .width(8), .enable("false")) multiplexer_8 (
    .in0(DataInput), .in1(in_14), .in2({8{1'b0}}), .in3({8{1'b0}}), .out(multiplexer_8_out),
    .sel({Reset, ROMoverwrite}));
  and and_8 (and_8_out, EnableWrite, decoder_1_out7);
  Multiplexer #(.select(2), .width(8), .enable("false")) multiplexer_9 (
    .in0(DataInput), .in1(in_15), .in2({8{1'b0}}), .in3({8{1'b0}}), .out(multiplexer_9_out),
    .sel({Reset, ROMoverwrite}));
  and and_9 (and_9_out, EnableWrite, decoder_1_out8);
  Multiplexer #(.select(2), .width(8), .enable("false")) multiplexer_10 (
    .in0(DataInput), .in1(in_16), .in2({8{1'b0}}), .in3({8{1'b0}}), .out(multiplexer_10_out),
    .sel({Reset, ROMoverwrite}));
  and and_10 (and_10_out, EnableWrite, decoder_1_out9);
  Multiplexer #(.select(2), .width(8), .enable("false")) multiplexer_11 (
    .in0(DataInput), .in1(in_17), .in2({8{1'b0}}), .in3({8{1'b0}}), .out(multiplexer_11_out),
    .sel({Reset, ROMoverwrite}));
  and and_11 (and_11_out, EnableWrite, decoder_1_out10);
  Multiplexer #(.select(2), .width(8), .enable("false")) multiplexer_12 (
    .in0(DataInput), .in1(in_18), .in2({8{1'b0}}), .in3({8{1'b0}}), .out(multiplexer_12_out),
    .sel({Reset, ROMoverwrite}));
  and and_12 (and_12_out, EnableWrite, decoder_1_out11);
  Multiplexer #(.select(2), .width(8), .enable("false")) multiplexer_13 (
    .in0(DataInput), .in1(in_19), .in2({8{1'b0}}), .in3({8{1'b0}}), .out(multiplexer_13_out),
    .sel({Reset, ROMoverwrite}));
  and and_13 (and_13_out, EnableWrite, decoder_1_out12);
  Multiplexer #(.select(2), .width(8), .enable("false")) multiplexer_14 (
    .in0(DataInput), .in1(in_20), .in2({8{1'b0}}), .in3({8{1'b0}}), .out(multiplexer_14_out),
    .sel({Reset, ROMoverwrite}));
  and and_14 (and_14_out, EnableWrite, decoder_1_out13);
  Multiplexer #(.select(2), .width(8), .enable("false")) multiplexer_15 (
    .in0(DataInput), .in1(in_21), .in2({8{1'b0}}), .in3({8{1'b0}}), .out(multiplexer_15_out),
    .sel({Reset, ROMoverwrite}));
  and and_15 (and_15_out, EnableWrite, decoder_1_out14);
  Multiplexer #(.select(2), .width(8), .enable("false")) multiplexer_16 (
    .in0(DataInput), .in1(in_22), .in2({8{1'b0}}), .in3({8{1'b0}}), .out(multiplexer_16_out),
    .sel({Reset, ROMoverwrite}));
  and and_16 (and_16_out, EnableWrite, decoder_1_out15);
  Decoder #(.select(4), .enable("false")) decoder_1 (
    .out0(decoder_1_out0), .out1(decoder_1_out1), .out2(decoder_1_out2), .out3(decoder_1_out3),
    .out4(decoder_1_out4), .out5(decoder_1_out5), .out6(decoder_1_out6), .out7(decoder_1_out7),
    .out8(decoder_1_out8), .out9(decoder_1_out9), .out10(decoder_1_out10), .out11(decoder_1_out11),
    .out12(decoder_1_out12), .out13(decoder_1_out13), .out14(decoder_1_out14), .out15(decoder_1_out15),
    .sel(Addr));
  byte_storage_compact byte_storage_compact_1 (
    .dataout(out_24), .datain(multiplexer_1_out), .EnableWrite(or_1_out), .Clock(CLK));
  byte_storage_compact byte_storage_compact_2 (
    .dataout(out_25), .datain(multiplexer_2_out), .EnableWrite(or_2_out), .Clock(CLK));
  byte_storage_compact byte_storage_compact_3 (
    .dataout(out_26), .datain(multiplexer_3_out), .EnableWrite(or_3_out), .Clock(CLK));
  byte_storage_compact byte_storage_compact_4 (
    .dataout(out_27), .datain(multiplexer_4_out), .EnableWrite(or_4_out), .Clock(CLK));
  byte_storage_compact byte_storage_compact_5 (
    .dataout(out_28), .datain(multiplexer_5_out), .EnableWrite(or_5_out), .Clock(CLK));
  byte_storage_compact byte_storage_compact_6 (
    .dataout(out_29), .datain(multiplexer_6_out), .EnableWrite(or_6_out), .Clock(CLK));
  byte_storage_compact byte_storage_compact_7 (
    .dataout(out_30), .datain(multiplexer_7_out), .EnableWrite(or_7_out), .Clock(CLK));
  byte_storage_compact byte_storage_compact_8 (
    .dataout(out_31), .datain(multiplexer_8_out), .EnableWrite(or_8_out), .Clock(CLK));
  byte_storage_compact byte_storage_compact_9 (
    .dataout(out_32), .datain(multiplexer_9_out), .EnableWrite(or_9_out), .Clock(CLK));
  byte_storage_compact byte_storage_compact_10 (
    .dataout(out_33), .datain(multiplexer_10_out), .EnableWrite(or_10_out), .Clock(CLK));
  byte_storage_compact byte_storage_compact_11 (
    .dataout(out_34), .datain(multiplexer_11_out), .EnableWrite(or_11_out), .Clock(CLK));
  byte_storage_compact byte_storage_compact_12 (
    .dataout(out_35), .datain(multiplexer_12_out), .EnableWrite(or_12_out), .Clock(CLK));
  byte_storage_compact byte_storage_compact_13 (
    .dataout(out_36), .datain(multiplexer_13_out), .EnableWrite(or_13_out), .Clock(CLK));
  byte_storage_compact byte_storage_compact_14 (
    .dataout(out_37), .datain(multiplexer_14_out), .EnableWrite(or_14_out), .Clock(CLK));
  byte_storage_compact byte_storage_compact_15 (
    .dataout(out_38), .datain(multiplexer_15_out), .EnableWrite(or_15_out), .Clock(CLK));
  byte_storage_compact byte_storage_compact_16 (
    .dataout(out_39), .datain(multiplexer_16_out), .EnableWrite(or_16_out), .Clock(CLK));
  Multiplexer #(.select(4), .width(8), .enable("false")) multiplexer_17 (
    .in0(out_24), .in1(out_25), .in2(out_26), .in3(out_27), .in4(out_28), .in5(out_29), .in6(out_30),
    .in7(out_31), .in8(out_32), .in9(out_33), .in10(out_34), .in11(out_35), .in12(out_36), .in13(out_37),
    .in14(out_38), .in15(out_39), .out(out_23), .sel(Addr));
endmodule

module ROM16C (
  input  Enable,
  input  [7:0] in_2,
  input  [7:0] in_3,
  input  [7:0] in_4,
  input  [7:0] in_5,
  input  [7:0] in_6,
  input  [7:0] in_7,
  input  [7:0] in_8,
  input  [7:0] in_9,
  input  [7:0] in_10,
  input  [7:0] in_11,
  input  [7:0] in_12,
  input  [7:0] in_13,
  input  [7:0] in_14,
  input  [7:0] in_15,
  input  [7:0] in_16,
  input  [7:0] in_17,
  output out_18,
  output [7:0] out_19,
  output [7:0] out_20,
  output [7:0] out_21,
  output [7:0] out_22,
  output [7:0] out_23,
  output [7:0] out_24,
  output [7:0] out_25,
  output [7:0] out_26,
  output [7:0] out_27,
  output [7:0] out_28,
  output [7:0] out_29,
  output [7:0] out_30,
  output [7:0] out_31,
  output [7:0] out_32,
  output [7:0] out_33,
  output [7:0] out_34
);


  assign out_18 = Enable;
  assign out_19 = in_2;
  assign out_20 = in_3;
  assign out_21 = in_4;
  assign out_22 = in_5;
  assign out_23 = in_6;
  assign out_24 = in_7;
  assign out_25 = in_8;
  assign out_26 = in_9;
  assign out_27 = in_10;
  assign out_28 = in_11;
  assign out_29 = in_12;
  assign out_30 = in_13;
  assign out_31 = in_14;
  assign out_32 = in_15;
  assign out_33 = in_16;
  assign out_34 = in_17;
endmodule

module four_bit_storage (
  input  [3:0] In1,
  input  Clock,
  input  Write,
  output [3:0] Out1
);

  wire and_1_out;

  D_Flip_Flop d_ff_1 (.D(In1[0]), .clk(and_1_out), .Q(Out1[0]));  // open: Qn, preset, reset
  and and_1 (and_1_out, Clock, Write);
  D_Flip_Flop d_ff_2 (.D(In1[1]), .clk(and_1_out), .Q(Out1[1]));  // open: Qn, preset, reset
  D_Flip_Flop d_ff_3 (.D(In1[2]), .clk(and_1_out), .Q(Out1[2]));  // open: Qn, preset, reset
  D_Flip_Flop d_ff_4 (.D(In1[3]), .clk(and_1_out), .Q(Out1[3]));  // open: Qn, preset, reset
endmodule

module data_registers (
  input  Clk,
  input  Rw,
  input  Which,
  input  [7:0] DataInput,
  output [7:0] DataOutput,
  output Eq
);

  wire and_1_out, and_2_out, xnor_1_out, xnor_2_out, xnor_3_out, xnor_4_out, xnor_5_out, xnor_6_out,
       xnor_7_out, xnor_8_out;
  wire [7:0] byte_storage_compact_1_dataout, byte_storage_compact_2_dataout;

  xnor xnor_1 (xnor_1_out, byte_storage_compact_2_dataout[7], byte_storage_compact_1_dataout[7]);
  xnor xnor_2 (xnor_2_out, byte_storage_compact_2_dataout[6], byte_storage_compact_1_dataout[6]);
  and and_1 (and_1_out, Rw, ~Which);  // AND_Gate
  and and_2 (and_2_out, Rw, Which);
  xnor xnor_3 (xnor_3_out, byte_storage_compact_2_dataout[4], byte_storage_compact_1_dataout[4]);
  xnor xnor_4 (xnor_4_out, byte_storage_compact_2_dataout[5], byte_storage_compact_1_dataout[5]);
  byte_storage_compact byte_storage_compact_1 (
    .dataout(byte_storage_compact_1_dataout), .datain(DataInput), .EnableWrite(and_1_out), .Clock(Clk));
  byte_storage_compact byte_storage_compact_2 (
    .dataout(byte_storage_compact_2_dataout), .datain(DataInput), .EnableWrite(and_2_out), .Clock(Clk));
  xnor xnor_5 (xnor_5_out, byte_storage_compact_2_dataout[3], byte_storage_compact_1_dataout[3]);
  Multiplexer #(.width(8), .enable("false")) multiplexer_1 (
    .in0(byte_storage_compact_1_dataout), .in1(byte_storage_compact_2_dataout), .out(DataOutput), .sel(Which));
  xnor xnor_6 (xnor_6_out, byte_storage_compact_2_dataout[2], byte_storage_compact_1_dataout[2]);
  xnor xnor_7 (xnor_7_out, byte_storage_compact_2_dataout[1], byte_storage_compact_1_dataout[1]);
  xnor xnor_8 (xnor_8_out, byte_storage_compact_2_dataout[0], byte_storage_compact_1_dataout[0]);
  and and_3 (Eq, xnor_8_out, xnor_7_out, xnor_6_out, xnor_5_out, xnor_3_out, xnor_4_out, xnor_2_out, xnor_1_out);
endmodule
